// Logisim project 8bit_Computer_Roki10.circ as structural Verilog: 1 circuit, main circuit main
module main (
  input  Hold,
  input  Ram_Of,
  input  Ram_In,
  input  Ram_out,
  input  IR_In,
  input  IR_out,
  input  A_In,
  input  A_out,
  input  B_In,
  input  B_out,
  input  C_In,
  input  C_out,
  input  [3:0] PC_Input,
  input  PC_En,
  input  PC_out,
  input  PC_jump,
  input  PC_clr,
  input  M_In,
  input  M_out,
  input  OR_in,
  input  [7:0] M__Input,
  input  Disp_of,
  input  ALU_out,
  input  A_B,
  input  In__AR,
  input  B__AR,
  input  [3:0] AR_Input,
  input  [7:0] in_28,
  output c_out_2,
  output [7:0] sum,
  output out_31
);

  wire adder_3_cout, adder_4_cout, adder_5_cout, adder_6_cout, adder_7_cout, adder_8_cout, adder_9_cout,
       adder_10_cout, adder_11_cout, adder_12_cout, adder_13_cout, adder_14_cout, adder_15_cout,
       adder_16_cout, and_2_out, and_3_out, and_4_out, and_5_out, and_6_out, and_7_out, and_8_out, and_9_out,
       and_10_out, and_11_out, and_12_out, and_13_out, and_14_out, and_15_out, and_16_out, and_17_out,
       and_18_out, button_1_out, clock_1_out, decoder_1_out0, decoder_1_out1, decoder_1_out2, decoder_1_out3,
       decoder_1_out4, decoder_1_out5, decoder_1_out6, decoder_1_out7, decoder_1_out8, decoder_1_out9,
       decoder_1_out10, decoder_1_out11, decoder_1_out12, decoder_1_out13, decoder_1_out14, decoder_1_out15,
       n7408_1_pin8, n74138_1_pin4, n74138_1_pin6, n74138_1_pin10, n74138_1_pin11, n74138_1_pin12,
       n74138_1_pin13, n74138_1_pin14, n74138_1_pin15, n74157_1_pin8, n74157_1_pin16, n74161_1_pin1,
       n74161_1_pin8, n74161_1_pin9, n74161_1_pin16, n74163_1_pin1, n74163_1_pin7, n74163_1_pin8,
       n74245_1_pin1, n74245_1_pin10, n74245_1_pin19, n74245_2_pin19, n74245_3_pin19, n74245_4_pin19,
       n74245_5_pin19, n74245_6_pin19, n74245_7_pin19, n74245_8_pin19, n74245_9_pin19, n74245_10_pin19,
       n74245_11_pin19, n74245_12_pin19, n74245_13_pin19, n74245_14_pin19, n74245_15_pin19, n74245_16_pin19,
       n74245_17_pin1, n74245_17_pin10, n74245_17_pin19, n74245_18_pin1, n74245_18_pin11, n74245_18_pin12,
       n74245_18_pin13, n74245_18_pin14, n74245_18_pin18, n74245_18_pin19, n74245_18_pin20, n74245_19_pin1,
       n74245_19_pin6, n74245_19_pin19, n74245_20_pin1, n74245_20_pin10, n74245_21_pin1, n74245_21_pin10,
       n74245_21_pin19, n74245_22_pin1, n74245_22_pin6, n74245_23_pin1, n74245_23_pin10, n74245_24_pin1,
       n74245_24_pin10, n74273_1_pin1, not_1_out, not_2_out, not_4_out, not_7_out, not_10_out, not_11_out,
       not_12_out, not_14_out, not_16_out, pull_resistor_2_node, pull_resistor_18_node, switch_1_p2,
       switch_2_p1, switch_2_p2, transistor_1_out, transistor_3_out, transistor_4_out, xor_1_out, xor_2_out,
       xor_3_out, xor_4_out, xor_5_out, xor_6_out, xor_7_out, xor_8_out, xor_9_out, xor_10_out, xor_11_out,
       xor_12_out, xor_13_out, xor_14_out, xor_15_out, xor_16_out;
  wire [2:0] n74163_1_pin14;
  wire [3:0] n74245_22_pin18, pull_resistor_8_node;
  wire [6:6] not_8_out;
  wire [7:0] n74245_1_pin18, n74245_17_pin2, n74273_1_pin2, register_1_q, register_2_q, register_3_q,
       register_4_q, register_5_q, register_6_q, register_7_q, register_8_q, register_9_q, register_10_q,
       register_11_q, register_12_q, register_13_q, register_14_q, register_15_q, register_16_q,
       register_17_q, register_18_q, register_19_q, register_20_q, register_21_q, register_22_q,
       register_23_q;
  wire [15:0] rom_1_data;
  wire [31:0] rom_2_data;

  Clock clock_1 (.out(clock_1_out));
  not not_1 (not_1_out, transistor_1_out);
  // Switch switch_1: pin names not known; wires that end beside it: clock_1_out, switch_1_p2
  Pull_Resistor pull_resistor_1 (.node(switch_1_p2));
  Transistor transistor_1 (.in(clock_1_out), .out(transistor_1_out), .gate(switch_1_p2));
  Pull_Resistor pull_resistor_2 (.node(pull_resistor_2_node));
  Transistor transistor_2 (.in(1'b1), .out(transistor_1_out), .gate(pull_resistor_2_node));
  _74163 #(.ShowInternalStructure("true"), .VccGndPorts("true")) u_74163_1 (
    .pin1(n74163_1_pin1), .pin2(not_1_out), .pin7(n74163_1_pin7), .pin8(n74163_1_pin8),
    .pin16(n74163_1_pin7), .pin14(n74163_1_pin14[0]), .pin13(n74163_1_pin14[1]), .pin12(n74163_1_pin14[2]),
    .pin10(n74163_1_pin7));  // open: pin3, pin4, pin5, pin6, pin15, pin11, pin9
  and and_1 (n74163_1_pin1, transistor_3_out, n74138_1_pin11);
  Button button_1 (.out(button_1_out));
  Transistor transistor_3 (.in(1'b1), .out(transistor_3_out), .gate(button_1_out));
  Pull_Resistor pull_resistor_3 (.node(transistor_3_out));
  Pull_Resistor pull_resistor_4 (.node(transistor_1_out));
  LED led_1 (.in(register_18_q[7]));
  LED led_2 (.in(register_18_q[6]));
  LED led_3 (.in(register_18_q[5]));
  not not_2 (not_2_out, transistor_3_out);
  Register register_1 (.D(n74245_1_pin18), .en(and_2_out), .clk(transistor_4_out), .Q(register_1_q));  // open: clr
  Register register_2 (.D(n74245_1_pin18), .en(and_3_out), .clk(transistor_4_out), .Q(register_2_q));  // open: clr
  Register register_3 (.D(n74245_1_pin18), .en(and_4_out), .clk(transistor_4_out), .Q(register_3_q));  // open: clr
  Register register_4 (.D(n74245_1_pin18), .en(and_5_out), .clk(transistor_4_out), .Q(register_4_q));  // open: clr
  Register register_5 (.D(n74245_1_pin18), .en(and_6_out), .clk(transistor_4_out), .Q(register_5_q));  // open: clr
  Register register_6 (.D(n74245_1_pin18), .en(and_7_out), .clk(transistor_4_out), .Q(register_6_q));  // open: clr
  Register register_7 (.D(n74245_1_pin18), .en(and_8_out), .clk(transistor_4_out), .Q(register_7_q));  // open: clr
  Register register_8 (.D(n74245_1_pin18), .en(and_9_out), .clk(transistor_4_out), .Q(register_8_q));  // open: clr
  Register register_9 (.D(n74245_1_pin18), .en(and_10_out), .clk(transistor_4_out), .Q(register_9_q));  // open: clr
  Register register_10 (.D(n74245_1_pin18), .en(and_11_out), .clk(transistor_4_out), .Q(register_10_q));  // open: clr
  Register register_11 (.D(n74245_1_pin18), .en(and_12_out), .clk(transistor_4_out), .Q(register_11_q));  // open: clr
  Register register_12 (.D(n74245_1_pin18), .en(and_13_out), .clk(transistor_4_out), .Q(register_12_q));  // open: clr
  Register register_13 (.D(n74245_1_pin18), .en(and_14_out), .clk(transistor_4_out), .Q(register_13_q));  // open: clr
  Register register_14 (.D(n74245_1_pin18), .en(and_15_out), .clk(transistor_4_out), .Q(register_14_q));  // open: clr
  Register register_15 (.D(n74245_1_pin18), .en(and_16_out), .clk(transistor_4_out), .Q(register_15_q));  // open: clr
  Register register_16 (.D(n74245_1_pin18), .en(and_17_out), .clk(transistor_4_out), .Q(register_16_q));  // open: clr
  LED led_4 (.in(transistor_1_out));
  not not_3 (pull_resistor_2_node, rom_1_data[14]);
  LED led_5 (.in(register_18_q[4]));
  LED led_6 (.in(n74163_1_pin14[2]));
  LED led_7 (.in(n74163_1_pin14[1]));
  _74245 #(.ShowInternalStructure("true"), .VccGndPorts("true")) u_74245_1 (
    .pin1(n74245_1_pin1), .pin2(register_1_q[0]), .pin3(register_1_q[1]), .pin4(register_1_q[2]),
    .pin5(register_1_q[3]), .pin6(register_1_q[4]), .pin7(register_1_q[5]), .pin8(register_1_q[6]),
    .pin9(register_1_q[7]), .pin10(n74245_1_pin10), .pin20(n74245_1_pin1), .pin19(n74245_1_pin19),
    .pin18(n74245_1_pin18[0]), .pin17(n74245_1_pin18[1]), .pin16(n74245_1_pin18[2]),
    .pin15(n74245_1_pin18[3]), .pin14(n74245_1_pin18[4]), .pin13(n74245_1_pin18[5]),
    .pin12(n74245_1_pin18[6]), .pin11(n74245_1_pin18[7]));
  _74245 #(.ShowInternalStructure("true"), .VccGndPorts("true")) u_74245_2 (
    .pin1(n74245_1_pin1), .pin2(register_2_q[0]), .pin3(register_2_q[1]), .pin4(register_2_q[2]),
    .pin5(register_2_q[3]), .pin6(register_2_q[4]), .pin7(register_2_q[5]), .pin8(register_2_q[6]),
    .pin9(register_2_q[7]), .pin10(n74245_1_pin10), .pin20(n74245_1_pin1), .pin19(n74245_2_pin19),
    .pin18(n74245_1_pin18[0]), .pin17(n74245_1_pin18[1]), .pin16(n74245_1_pin18[2]),
    .pin15(n74245_1_pin18[3]), .pin14(n74245_1_pin18[4]), .pin13(n74245_1_pin18[5]),
    .pin12(n74245_1_pin18[6]), .pin11(n74245_1_pin18[7]));
  _74245 #(.ShowInternalStructure("true"), .VccGndPorts("true")) u_74245_3 (
    .pin1(n74245_1_pin1), .pin2(register_3_q[0]), .pin3(register_3_q[1]), .pin4(register_3_q[2]),
    .pin5(register_3_q[3]), .pin6(register_3_q[4]), .pin7(register_3_q[5]), .pin8(register_3_q[6]),
    .pin9(register_3_q[7]), .pin10(n74245_1_pin10), .pin20(n74245_1_pin1), .pin19(n74245_3_pin19),
    .pin18(n74245_1_pin18[0]), .pin17(n74245_1_pin18[1]), .pin16(n74245_1_pin18[2]),
    .pin15(n74245_1_pin18[3]), .pin14(n74245_1_pin18[4]), .pin13(n74245_1_pin18[5]),
    .pin12(n74245_1_pin18[6]), .pin11(n74245_1_pin18[7]));
  _74245 #(.ShowInternalStructure("true"), .VccGndPorts("true")) u_74245_4 (
    .pin1(n74245_1_pin1), .pin2(register_4_q[0]), .pin3(register_4_q[1]), .pin4(register_4_q[2]),
    .pin5(register_4_q[3]), .pin6(register_4_q[4]), .pin7(register_4_q[5]), .pin8(register_4_q[6]),
    .pin9(register_4_q[7]), .pin10(n74245_1_pin10), .pin20(n74245_1_pin1), .pin19(n74245_4_pin19),
    .pin18(n74245_1_pin18[0]), .pin17(n74245_1_pin18[1]), .pin16(n74245_1_pin18[2]),
    .pin15(n74245_1_pin18[3]), .pin14(n74245_1_pin18[4]), .pin13(n74245_1_pin18[5]),
    .pin12(n74245_1_pin18[6]), .pin11(n74245_1_pin18[7]));
  _74245 #(.ShowInternalStructure("true"), .VccGndPorts("true")) u_74245_5 (
    .pin1(n74245_1_pin1), .pin2(register_5_q[0]), .pin3(register_5_q[1]), .pin4(register_5_q[2]),
    .pin5(register_5_q[3]), .pin6(register_5_q[4]), .pin7(register_5_q[5]), .pin8(register_5_q[6]),
    .pin9(register_5_q[7]), .pin10(n74245_1_pin10), .pin20(n74245_1_pin1), .pin19(n74245_5_pin19),
    .pin18(n74245_1_pin18[0]), .pin17(n74245_1_pin18[1]), .pin16(n74245_1_pin18[2]),
    .pin15(n74245_1_pin18[3]), .pin14(n74245_1_pin18[4]), .pin13(n74245_1_pin18[5]),
    .pin12(n74245_1_pin18[6]), .pin11(n74245_1_pin18[7]));
  _74245 #(.ShowInternalStructure("true"), .VccGndPorts("true")) u_74245_6 (
    .pin1(n74245_1_pin1), .pin2(register_6_q[0]), .pin3(register_6_q[1]), .pin4(register_6_q[2]),
    .pin5(register_6_q[3]), .pin6(register_6_q[4]), .pin7(register_6_q[5]), .pin8(register_6_q[6]),
    .pin9(register_6_q[7]), .pin10(n74245_1_pin10), .pin20(n74245_1_pin1), .pin19(n74245_6_pin19),
    .pin18(n74245_1_pin18[0]), .pin17(n74245_1_pin18[1]), .pin16(n74245_1_pin18[2]),
    .pin15(n74245_1_pin18[3]), .pin14(n74245_1_pin18[4]), .pin13(n74245_1_pin18[5]),
    .pin12(n74245_1_pin18[6]), .pin11(n74245_1_pin18[7]));
  _74245 #(.ShowInternalStructure("true"), .VccGndPorts("true")) u_74245_7 (
    .pin1(n74245_1_pin1), .pin2(register_7_q[0]), .pin3(register_7_q[1]), .pin4(register_7_q[2]),
    .pin5(register_7_q[3]), .pin6(register_7_q[4]), .pin7(register_7_q[5]), .pin8(register_7_q[6]),
    .pin9(register_7_q[7]), .pin10(n74245_1_pin10), .pin20(n74245_1_pin1), .pin19(n74245_7_pin19),
    .pin18(n74245_1_pin18[0]), .pin17(n74245_1_pin18[1]), .pin16(n74245_1_pin18[2]),
    .pin15(n74245_1_pin18[3]), .pin14(n74245_1_pin18[4]), .pin13(n74245_1_pin18[5]),
    .pin12(n74245_1_pin18[6]), .pin11(n74245_1_pin18[7]));
  _74245 #(.ShowInternalStructure("true"), .VccGndPorts("true")) u_74245_8 (
    .pin1(n74245_1_pin1), .pin2(register_8_q[0]), .pin3(register_8_q[1]), .pin4(register_8_q[2]),
    .pin5(register_8_q[3]), .pin6(register_8_q[4]), .pin7(register_8_q[5]), .pin8(register_8_q[6]),
    .pin9(register_8_q[7]), .pin10(n74245_1_pin10), .pin20(n74245_1_pin1), .pin19(n74245_8_pin19),
    .pin18(n74245_1_pin18[0]), .pin17(n74245_1_pin18[1]), .pin16(n74245_1_pin18[2]),
    .pin15(n74245_1_pin18[3]), .pin14(n74245_1_pin18[4]), .pin13(n74245_1_pin18[5]),
    .pin12(n74245_1_pin18[6]), .pin11(n74245_1_pin18[7]));
  _74245 #(.ShowInternalStructure("true"), .VccGndPorts("true")) u_74245_9 (
    .pin1(n74245_1_pin1), .pin2(register_9_q[0]), .pin3(register_9_q[1]), .pin4(register_9_q[2]),
    .pin5(register_9_q[3]), .pin6(register_9_q[4]), .pin7(register_9_q[5]), .pin8(register_9_q[6]),
    .pin9(register_9_q[7]), .pin10(n74245_1_pin10), .pin20(n74245_1_pin1), .pin19(n74245_9_pin19),
    .pin18(n74245_1_pin18[0]), .pin17(n74245_1_pin18[1]), .pin16(n74245_1_pin18[2]),
    .pin15(n74245_1_pin18[3]), .pin14(n74245_1_pin18[4]), .pin13(n74245_1_pin18[5]),
    .pin12(n74245_1_pin18[6]), .pin11(n74245_1_pin18[7]));
  _74245 #(.ShowInternalStructure("true"), .VccGndPorts("true")) u_74245_10 (
    .pin1(n74245_1_pin1), .pin2(register_10_q[0]), .pin3(register_10_q[1]), .pin4(register_10_q[2]),
    .pin5(register_10_q[3]), .pin6(register_10_q[4]), .pin7(register_10_q[5]), .pin8(register_10_q[6]),
    .pin9(register_10_q[7]), .pin10(n74245_1_pin10), .pin20(n74245_1_pin1), .pin19(n74245_10_pin19),
    .pin18(n74245_1_pin18[0]), .pin17(n74245_1_pin18[1]), .pin16(n74245_1_pin18[2]),
    .pin15(n74245_1_pin18[3]), .pin14(n74245_1_pin18[4]), .pin13(n74245_1_pin18[5]),
    .pin12(n74245_1_pin18[6]), .pin11(n74245_1_pin18[7]));
  _74245 #(.ShowInternalStructure("true"), .VccGndPorts("true")) u_74245_11 (
    .pin1(n74245_1_pin1), .pin2(register_11_q[0]), .pin3(register_11_q[1]), .pin4(register_11_q[2]),
    .pin5(register_11_q[3]), .pin6(register_11_q[4]), .pin7(register_11_q[5]), .pin8(register_11_q[6]),
    .pin9(register_11_q[7]), .pin10(n74245_1_pin10), .pin20(n74245_1_pin1), .pin19(n74245_11_pin19),
    .pin18(n74245_1_pin18[0]), .pin17(n74245_1_pin18[1]), .pin16(n74245_1_pin18[2]),
    .pin15(n74245_1_pin18[3]), .pin14(n74245_1_pin18[4]), .pin13(n74245_1_pin18[5]),
    .pin12(n74245_1_pin18[6]), .pin11(n74245_1_pin18[7]));
  _74245 #(.ShowInternalStructure("true"), .VccGndPorts("true")) u_74245_12 (
    .pin1(n74245_1_pin1), .pin2(register_12_q[0]), .pin3(register_12_q[1]), .pin4(register_12_q[2]),
    .pin5(register_12_q[3]), .pin6(register_12_q[4]), .pin7(register_12_q[5]), .pin8(register_12_q[6]),
    .pin9(register_12_q[7]), .pin10(n74245_1_pin10), .pin20(n74245_1_pin1), .pin19(n74245_12_pin19),
    .pin18(n74245_1_pin18[0]), .pin17(n74245_1_pin18[1]), .pin16(n74245_1_pin18[2]),
    .pin15(n74245_1_pin18[3]), .pin14(n74245_1_pin18[4]), .pin13(n74245_1_pin18[5]),
    .pin12(n74245_1_pin18[6]), .pin11(n74245_1_pin18[7]));
  _74245 #(.ShowInternalStructure("true"), .VccGndPorts("true")) u_74245_13 (
    .pin1(n74245_1_pin1), .pin2(register_13_q[0]), .pin3(register_13_q[1]), .pin4(register_13_q[2]),
    .pin5(register_13_q[3]), .pin6(register_13_q[4]), .pin7(register_13_q[5]), .pin8(register_13_q[6]),
    .pin9(register_13_q[7]), .pin10(n74245_1_pin10), .pin20(n74245_1_pin1), .pin19(n74245_13_pin19),
    .pin18(n74245_1_pin18[0]), .pin17(n74245_1_pin18[1]), .pin16(n74245_1_pin18[2]),
    .pin15(n74245_1_pin18[3]), .pin14(n74245_1_pin18[4]), .pin13(n74245_1_pin18[5]),
    .pin12(n74245_1_pin18[6]), .pin11(n74245_1_pin18[7]));
  _74245 #(.ShowInternalStructure("true"), .VccGndPorts("true")) u_74245_14 (
    .pin1(n74245_1_pin1), .pin2(register_14_q[0]), .pin3(register_14_q[1]), .pin4(register_14_q[2]),
    .pin5(register_14_q[3]), .pin6(register_14_q[4]), .pin7(register_14_q[5]), .pin8(register_14_q[6]),
    .pin9(register_14_q[7]), .pin10(n74245_1_pin10), .pin20(n74245_1_pin1), .pin19(n74245_14_pin19),
    .pin18(n74245_1_pin18[0]), .pin17(n74245_1_pin18[1]), .pin16(n74245_1_pin18[2]),
    .pin15(n74245_1_pin18[3]), .pin14(n74245_1_pin18[4]), .pin13(n74245_1_pin18[5]),
    .pin12(n74245_1_pin18[6]), .pin11(n74245_1_pin18[7]));
  _74245 #(.ShowInternalStructure("true"), .VccGndPorts("true")) u_74245_15 (
    .pin1(n74245_1_pin1), .pin2(register_15_q[0]), .pin3(register_15_q[1]), .pin4(register_15_q[2]),
    .pin5(register_15_q[3]), .pin6(register_15_q[4]), .pin7(register_15_q[5]), .pin8(register_15_q[6]),
    .pin9(register_15_q[7]), .pin10(n74245_1_pin10), .pin20(n74245_1_pin1), .pin19(n74245_15_pin19),
    .pin18(n74245_1_pin18[0]), .pin17(n74245_1_pin18[1]), .pin16(n74245_1_pin18[2]),
    .pin15(n74245_1_pin18[3]), .pin14(n74245_1_pin18[4]), .pin13(n74245_1_pin18[5]),
    .pin12(n74245_1_pin18[6]), .pin11(n74245_1_pin18[7]));
  _74245 #(.ShowInternalStructure("true"), .VccGndPorts("true")) u_74245_16 (
    .pin1(n74245_1_pin1), .pin2(register_16_q[0]), .pin3(register_16_q[1]), .pin4(register_16_q[2]),
    .pin5(register_16_q[3]), .pin6(register_16_q[4]), .pin7(register_16_q[5]), .pin8(register_16_q[6]),
    .pin9(register_16_q[7]), .pin10(n74245_1_pin10), .pin20(n74245_1_pin1), .pin19(n74245_16_pin19),
    .pin18(n74245_1_pin18[0]), .pin17(n74245_1_pin18[1]), .pin16(n74245_1_pin18[2]),
    .pin15(n74245_1_pin18[3]), .pin14(n74245_1_pin18[4]), .pin13(n74245_1_pin18[5]),
    .pin12(n74245_1_pin18[6]), .pin11(n74245_1_pin18[7]));
  LED led_8 (.in(n74163_1_pin14[0]));
  LED led_9 (.in(n74138_1_pin15));
  _74138 #(.ShowInternalStructure("true"), .VccGndPorts("true")) u_74138_1 (
    .pin1(n74163_1_pin14[0]), .pin2(n74163_1_pin14[1]), .pin3(n74163_1_pin14[2]), .pin4(n74138_1_pin4),
    .pin5(n74138_1_pin4), .pin6(n74138_1_pin6), .pin8(n74138_1_pin4), .pin16(n74138_1_pin6),
    .pin15(n74138_1_pin15), .pin14(n74138_1_pin14), .pin13(n74138_1_pin13), .pin12(n74138_1_pin12),
    .pin11(n74138_1_pin11), .pin10(n74138_1_pin10));  // open: pin7, pin9
  LED led_10 (.in(n74138_1_pin14));
  LED led_11 (.in(n74138_1_pin13));
  LED led_12 (.in(n74138_1_pin12));
  LED led_13 (.in(n74138_1_pin11));
  LED led_14 (.in(n74138_1_pin10));
  nand nand_1 (n74245_1_pin19, rom_1_data[11], decoder_1_out0);
  and and_2 (and_2_out, rom_1_data[12], decoder_1_out0);
  nand nand_2 (n74245_2_pin19, rom_1_data[11], decoder_1_out1);
  and and_3 (and_3_out, rom_1_data[12], decoder_1_out1);
  nand nand_3 (n74245_3_pin19, rom_1_data[11], decoder_1_out2);
  and and_4 (and_4_out, rom_1_data[12], decoder_1_out2);
  nand nand_4 (n74245_4_pin19, rom_1_data[11], decoder_1_out3);
  and and_5 (and_5_out, rom_1_data[12], decoder_1_out3);
  nand nand_5 (n74245_5_pin19, rom_1_data[11], decoder_1_out4);
  and and_6 (and_6_out, rom_1_data[12], decoder_1_out4);
  nand nand_6 (n74245_6_pin19, rom_1_data[11], decoder_1_out5);
  and and_7 (and_7_out, rom_1_data[12], decoder_1_out5);
  nand nand_7 (n74245_7_pin19, rom_1_data[11], decoder_1_out6);
  and and_8 (and_8_out, rom_1_data[12], decoder_1_out6);
  nand nand_8 (n74245_8_pin19, rom_1_data[11], decoder_1_out7);
  and and_9 (and_9_out, rom_1_data[12], decoder_1_out7);
  nand nand_9 (n74245_9_pin19, rom_1_data[11], decoder_1_out8);
  and and_10 (and_10_out, rom_1_data[12], decoder_1_out8);
  nand nand_10 (n74245_10_pin19, rom_1_data[11], decoder_1_out9);
  and and_11 (and_11_out, rom_1_data[12], decoder_1_out9);
  nand nand_11 (n74245_11_pin19, rom_1_data[11], decoder_1_out10);
  and and_12 (and_12_out, rom_1_data[12], decoder_1_out10);
  nand nand_12 (n74245_12_pin19, rom_1_data[11], decoder_1_out11);
  and and_13 (and_13_out, rom_1_data[12], decoder_1_out11);
  nand nand_13 (n74245_13_pin19, rom_1_data[11], decoder_1_out12);
  and and_14 (and_14_out, rom_1_data[12], decoder_1_out12);
  nand nand_14 (n74245_14_pin19, rom_1_data[11], decoder_1_out13);
  and and_15 (and_15_out, rom_1_data[12], decoder_1_out13);
  nand nand_15 (n74245_15_pin19, rom_1_data[11], decoder_1_out14);
  and and_16 (and_16_out, rom_1_data[12], decoder_1_out14);
  nand nand_16 (n74245_16_pin19, rom_1_data[11], decoder_1_out15);
  and and_17 (and_17_out, rom_1_data[12], decoder_1_out15);
  Decoder #(.disabled("Z"), .select(4)) decoder_1 (
    .out0(decoder_1_out0), .out1(decoder_1_out1), .out2(decoder_1_out2), .out3(decoder_1_out3),
    .out4(decoder_1_out4), .out5(decoder_1_out5), .out6(decoder_1_out6), .out7(decoder_1_out7),
    .out8(decoder_1_out8), .out9(decoder_1_out9), .out10(decoder_1_out10), .out11(decoder_1_out11),
    .out12(decoder_1_out12), .out13(decoder_1_out13), .out14(decoder_1_out14), .out15(decoder_1_out15),
    .sel(pull_resistor_8_node), .en(not_10_out));
  ROM #(.dataWidth(16)) rom_1 (.addr({1'b0, register_18_q[7:4], n74163_1_pin14}), .data(rom_1_data));
  ROM #(.dataWidth(32)) rom_2 (.addr(n74273_1_pin2), .data(rom_2_data));
  LED led_15 (.in(pull_resistor_8_node[3]));
  LED led_16 (.in(pull_resistor_8_node[2]));
  LED led_17 (.in(pull_resistor_8_node[1]));
  LED led_18 (.in(pull_resistor_8_node[0]));
  LED led_19 (.in(pull_resistor_8_node[3]));
  LED led_20 (.in(pull_resistor_8_node[2]));
  LED led_21 (.in(pull_resistor_8_node[1]));
  LED led_22 (.in(pull_resistor_8_node[0]));
  Pull_Resistor pull_resistor_5 (.node(pull_resistor_8_node[3]));
  Pull_Resistor pull_resistor_6 (.node(pull_resistor_8_node[2]));
  Pull_Resistor pull_resistor_7 (.node(pull_resistor_8_node[1]));
  Pull_Resistor pull_resistor_8 (.node(pull_resistor_8_node[0]));
  LED led_23 (.in(n74245_1_pin18[7]));
  LED led_24 (.in(n74245_1_pin18[6]));
  LED led_25 (.in(n74245_1_pin18[5]));
  LED led_26 (.in(n74245_1_pin18[4]));
  LED led_27 (.in(n74245_1_pin18[7]));
  LED led_28 (.in(n74245_1_pin18[6]));
  LED led_29 (.in(n74245_1_pin18[5]));
  LED led_30 (.in(n74245_1_pin18[4]));
  Pull_Resistor pull_resistor_9 (.node(n74245_1_pin18[7]));
  Pull_Resistor pull_resistor_10 (.node(n74245_1_pin18[6]));
  Pull_Resistor pull_resistor_11 (.node(n74245_1_pin18[5]));
  Pull_Resistor pull_resistor_12 (.node(n74245_1_pin18[4]));
  LED led_31 (.in(n74245_1_pin18[3]));
  LED led_32 (.in(n74245_1_pin18[2]));
  LED led_33 (.in(n74245_1_pin18[1]));
  LED led_34 (.in(n74245_1_pin18[0]));
  LED led_35 (.in(n74245_1_pin18[3]));
  LED led_36 (.in(n74245_1_pin18[2]));
  LED led_37 (.in(n74245_1_pin18[1]));
  LED led_38 (.in(n74245_1_pin18[0]));
  Pull_Resistor pull_resistor_13 (.node(n74245_1_pin18[3]));
  Pull_Resistor pull_resistor_14 (.node(n74245_1_pin18[2]));
  Pull_Resistor pull_resistor_15 (.node(n74245_1_pin18[1]));
  Pull_Resistor pull_resistor_16 (.node(n74245_1_pin18[0]));
  // Switch switch_2: pin names not known; wires that end beside it: switch_2_p1, switch_2_p2
  Pull_Resistor pull_resistor_17 (.node(switch_2_p2));
  Clock clock_2 (.out(switch_2_p1));
  Transistor transistor_4 (.in(switch_2_p1), .out(transistor_4_out), .gate(switch_2_p2));
  Pull_Resistor pull_resistor_18 (.node(pull_resistor_18_node));
  Transistor transistor_5 (.in(1'b1), .out(transistor_4_out), .gate(pull_resistor_18_node));
  LED led_39 (.in(n74245_1_pin18[7]));
  _74245 #(.ShowInternalStructure("true"), .VccGndPorts("true")) u_74245_17 (
    .pin1(n74245_17_pin1), .pin2(n74245_17_pin2[0]), .pin3(n74245_17_pin2[1]), .pin4(n74245_17_pin2[2]),
    .pin5(n74245_17_pin2[3]), .pin6(n74245_17_pin2[4]), .pin7(n74245_17_pin2[5]), .pin8(n74245_17_pin2[6]),
    .pin9(n74245_17_pin2[7]), .pin10(n74245_17_pin10), .pin20(n74245_17_pin1), .pin19(n74245_17_pin19),
    .pin18(n74245_1_pin18[0]), .pin17(n74245_1_pin18[1]), .pin16(n74245_1_pin18[2]),
    .pin15(n74245_1_pin18[3]), .pin14(n74245_1_pin18[4]), .pin13(n74245_1_pin18[5]),
    .pin12(n74245_1_pin18[6]), .pin11(n74245_1_pin18[7]));
  Pull_Resistor pull_resistor_19 (.node(transistor_4_out));
  LED led_40 (.in(n74245_1_pin18[6]));
  LED led_41 (.in(n74245_1_pin18[5]));
  LED led_42 (.in(n74245_1_pin18[4]));
  LED led_43 (.in(n74245_1_pin18[3]));
  not not_4 (not_4_out, Disp_of);
  LED led_44 (.in(transistor_4_out));
  not not_5 (pull_resistor_18_node, rom_1_data[14]);
  Register register_17 (
    .D(n74245_1_pin18), .en(rom_1_data[3]), .clk(transistor_4_out), .Q(register_17_q), .clr(not_2_out));
  _7408 #(.ShowInternalStructure("true")) u_7408_1 (
    .pin10(not_4_out), .pin9(transistor_4_out), .pin8(n7408_1_pin8));  // open: pin1, pin2, pin3, pin4, pin5, pin6, pin13, pin12, pin11
  Register register_18 (
    .D(n74245_1_pin18), .en(rom_1_data[9]), .clk(transistor_4_out), .Q(register_18_q), .clr(not_2_out));
  LED led_45 (.in(transistor_4_out));
  LED led_46 (.in(n74245_1_pin18[2]));
  LED led_47 (.in(n74245_1_pin18[1]));
  LED led_48 (.in(n74245_1_pin18[0]));
  LED led_49 (.in(transistor_4_out));
  LED led_50 (.in(Disp_of));
  not not_6 (n74245_17_pin19, rom_1_data[6]);
  LED led_51 (.in(register_18_q[7]));
  _74245 #(.ShowInternalStructure("true"), .VccGndPorts("true")) u_74245_18 (
    .pin1(n74245_18_pin1), .pin2(n74245_1_pin18[7]), .pin3(n74245_1_pin18[6]), .pin4(n74245_1_pin18[5]),
    .pin5(n74245_1_pin18[4]), .pin6(n74245_1_pin18[3]), .pin7(n74245_1_pin18[2]), .pin8(n74245_1_pin18[1]),
    .pin9(n74245_1_pin18[0]), .pin10(n74245_18_pin1), .pin20(n74245_18_pin20), .pin19(n74245_18_pin19),
    .pin18(n74245_18_pin18), .pin17(n74245_18_pin18), .pin16(n74245_18_pin18), .pin15(n74245_18_pin18),
    .pin14(n74245_18_pin14), .pin13(n74245_18_pin13), .pin12(n74245_18_pin12), .pin11(n74245_18_pin11));
  Register register_19 (.D(M__Input), .en(M_In), .clk(transistor_4_out), .Q(register_19_q), .clr(not_2_out));
  LED led_52 (.in(transistor_4_out));
  Register register_20 (.D(n74245_1_pin18), .en(C_In), .clk(transistor_4_out), .Q(register_20_q), .clr(not_2_out));
  LED led_53 (.in(rom_1_data[14]));
  LED led_54 (.in(rom_1_data[6]));
  not not_7 (not_7_out, In__AR);
  xor xor_1 (xor_1_out, register_23_q[7], rom_1_data[5]);
  not not_8 (not_8_out[6], and_18_out);
  _74273 #(.ShowInternalStructure("true")) u_74273_1 (
    .pin1(n74273_1_pin1), .pin2(n74273_1_pin2[0]), .pin3(register_17_q[0]), .pin4(register_17_q[1]),
    .pin5(n74273_1_pin2[1]), .pin6(n74273_1_pin2[2]), .pin7(register_17_q[2]), .pin8(register_17_q[3]),
    .pin9(n74273_1_pin2[3]), .pin19(n74273_1_pin2[6]), .pin18(register_17_q[7]), .pin17(register_17_q[6]),
    .pin16(n74273_1_pin2[7]), .pin15(n74273_1_pin2[5]), .pin14(register_17_q[5]), .pin13(register_17_q[4]),
    .pin12(n74273_1_pin2[4]), .pin11(n7408_1_pin8));
  not not_9 (n74273_1_pin1, not_2_out);
  LED led_55 (.in(register_18_q[0]));
  LED led_56 (.in(register_18_q[1]));
  LED led_57 (.in(register_18_q[2]));
  LED led_58 (.in(register_18_q[3]));
  LED led_59 (.in(register_18_q[6]));
  LED led_60 (.in(register_18_q[5]));
  LED led_61 (.in(register_18_q[4]));
  not not_10 (not_10_out, Ram_Of);
  LED led_62 (.in(Ram_Of));
  LED led_63 (.in(rom_1_data[5]));
  LED led_64 (.in(In__AR));
  xor xor_2 (xor_2_out, register_23_q[6], rom_1_data[5]);
  Adder #(.width(1)) adder_1 (.a(xor_1_out), .b(register_22_q[7]), .out(sum[7]), .cin(adder_3_cout), .cout(c_out_2));
  not not_11 (not_11_out, c_out_2);
  xor xor_3 (xor_3_out, sum[7], and_18_out);
  Adder #(.width(1)) adder_2 (.a(xor_3_out), .b(in_28[7]), .out(n74245_17_pin2[7]), .cin(adder_4_cout), .cout(out_31));
  _74245 #(.VccGndPorts("true")) u_74245_19 (
    .pin1(n74245_19_pin1), .pin2(register_18_q[0]), .pin3(register_18_q[1]), .pin4(register_18_q[2]),
    .pin5(register_18_q[3]), .pin6(n74245_19_pin6), .pin7(n74245_19_pin6), .pin8(n74245_19_pin6),
    .pin9(n74245_19_pin6), .pin10(n74245_19_pin6), .pin20(n74245_19_pin1), .pin19(n74245_19_pin19),
    .pin18(n74245_1_pin18[0]), .pin17(n74245_1_pin18[1]), .pin16(n74245_1_pin18[2]),
    .pin15(n74245_1_pin18[3]), .pin14(n74245_1_pin18[4]), .pin13(n74245_1_pin18[5]),
    .pin12(n74245_1_pin18[6]), .pin11(n74245_1_pin18[7]));
  LED led_65 (.in(register_19_q[0]));
  LED led_66 (.in(register_19_q[1]));
  LED led_67 (.in(register_19_q[2]));
  LED led_68 (.in(register_19_q[3]));
  LED led_69 (.in(register_19_q[4]));
  LED led_70 (.in(register_19_q[5]));
  LED led_71 (.in(register_19_q[6]));
  LED led_72 (.in(register_19_q[7]));
  LED led_73 (.in(register_20_q[0]));
  LED led_74 (.in(register_20_q[1]));
  LED led_75 (.in(register_20_q[2]));
  LED led_76 (.in(register_20_q[3]));
  LED led_77 (.in(register_20_q[4]));
  LED led_78 (.in(register_20_q[5]));
  LED led_79 (.in(register_20_q[6]));
  LED led_80 (.in(register_20_q[7]));
  LED led_81 (.in(rom_1_data[12]));
  not not_12 (not_12_out, M_out);
  LED led_82 (.in(M_In));
  LED led_83 (.in(rom_1_data[13]));
  xor xor_4 (xor_4_out, register_23_q[5], rom_1_data[5]);
  Adder #(.width(1)) adder_3 (
    .a(xor_2_out), .b(register_22_q[6]), .out(sum[6]), .cin(adder_5_cout), .cout(adder_3_cout));
  and and_18 (and_18_out, not_11_out, rom_1_data[5]);
  LED led_84 (.in(and_18_out));
  xor xor_5 (xor_5_out, sum[6], and_18_out);
  Adder #(.width(1)) adder_4 (
    .a(xor_5_out), .b(in_28[6]), .out(n74245_17_pin2[6]), .cin(adder_6_cout), .cout(adder_4_cout));
  _74161 #(.ShowInternalStructure("true"), .VccGndPorts("true")) u_74161_1 (
    .pin1(n74161_1_pin1), .pin2(transistor_4_out), .pin3(PC_Input[0]), .pin4(PC_Input[1]),
    .pin5(PC_Input[2]), .pin6(PC_Input[3]), .pin7(rom_1_data[2]), .pin8(n74161_1_pin8),
    .pin16(n74161_1_pin16), .pin14(n74245_18_pin11), .pin13(n74245_18_pin12), .pin12(n74245_18_pin13),
    .pin11(n74245_18_pin14), .pin10(rom_1_data[2]), .pin9(n74161_1_pin9));  // open: pin15
  _74245 #(.VccGndPorts("true")) u_74245_20 (
    .pin1(n74245_20_pin1), .pin2(register_19_q[0]), .pin3(register_19_q[1]), .pin4(register_19_q[2]),
    .pin5(register_19_q[3]), .pin6(register_19_q[4]), .pin7(register_19_q[5]), .pin8(register_19_q[6]),
    .pin9(register_19_q[7]), .pin10(n74245_20_pin10), .pin20(n74245_20_pin1), .pin19(not_12_out),
    .pin18(n74245_1_pin18[0]), .pin17(n74245_1_pin18[1]), .pin16(n74245_1_pin18[2]),
    .pin15(n74245_1_pin18[3]), .pin14(n74245_1_pin18[4]), .pin13(n74245_1_pin18[5]),
    .pin12(n74245_1_pin18[6]), .pin11(n74245_1_pin18[7]));
  _74245 #(.VccGndPorts("true")) u_74245_21 (
    .pin1(n74245_21_pin1), .pin2(register_20_q[0]), .pin3(register_20_q[1]), .pin4(register_20_q[2]),
    .pin5(register_20_q[3]), .pin6(register_20_q[4]), .pin7(register_20_q[5]), .pin8(register_20_q[6]),
    .pin9(register_20_q[7]), .pin10(n74245_21_pin10), .pin20(n74245_21_pin1), .pin19(n74245_21_pin19),
    .pin18(n74245_1_pin18[0]), .pin17(n74245_1_pin18[1]), .pin16(n74245_1_pin18[2]),
    .pin15(n74245_1_pin18[3]), .pin14(n74245_1_pin18[4]), .pin13(n74245_1_pin18[5]),
    .pin12(n74245_1_pin18[6]), .pin11(n74245_1_pin18[7]));
  LED led_85 (.in(rom_1_data[11]));
  LED led_86 (.in(M_out));
  xor xor_6 (xor_6_out, register_23_q[4], rom_1_data[5]);
  Adder #(.width(1)) adder_5 (
    .a(xor_4_out), .b(register_22_q[5]), .out(sum[5]), .cin(adder_7_cout), .cout(adder_5_cout));
  xor xor_7 (xor_7_out, sum[5], and_18_out);
  Adder #(.width(1)) adder_6 (
    .a(xor_7_out), .b(in_28[5]), .out(n74245_17_pin2[5]), .cin(adder_8_cout), .cout(adder_6_cout));
  LED led_87 (.in(rom_1_data[9]));
  LED led_88 (.in(rom_1_data[3]));
  xor xor_8 (xor_8_out, register_23_q[3], rom_1_data[5]);
  Adder #(.width(1)) adder_7 (
    .a(xor_6_out), .b(register_22_q[4]), .out(sum[4]), .cin(adder_9_cout), .cout(adder_7_cout));
  xor xor_9 (xor_9_out, sum[4], and_18_out);
  Adder #(.width(1)) adder_8 (
    .a(xor_9_out), .b(in_28[4]), .out(n74245_17_pin2[4]), .cin(adder_10_cout), .cout(adder_8_cout));
  _7_Segment_Display #(.active("false")) u_7_segment_display_1 (
    .g(not_8_out[6]), .f(1'b1), .a(1'b1), .b(1'b1), .e(1'b1), .d(1'b1), .c(1'b1), .dp(1'b1));
  _7_Segment_Display #(.active("false")) u_7_segment_display_2 (
    .g(rom_2_data[22]), .f(rom_2_data[21]), .a(rom_2_data[16]), .b(rom_2_data[17]), .e(rom_2_data[20]),
    .d(rom_2_data[19]), .c(rom_2_data[18]), .dp(rom_2_data[23]));
  not not_13 (n74245_19_pin19, rom_1_data[10]);
  LED led_89 (.in(rom_1_data[10]));
  LED led_90 (.in(rom_1_data[8]));
  xor xor_10 (xor_10_out, register_23_q[2], rom_1_data[5]);
  Adder #(.width(1)) adder_9 (
    .a(xor_8_out), .b(register_22_q[3]), .out(sum[3]), .cin(adder_11_cout), .cout(adder_9_cout));
  xor xor_11 (xor_11_out, sum[3], and_18_out);
  Adder #(.width(1)) adder_10 (
    .a(xor_11_out), .b(in_28[3]), .out(n74245_17_pin2[3]), .cin(adder_12_cout), .cout(adder_10_cout));
  _7_Segment_Display #(.active("false")) u_7_segment_display_3 (
    .g(rom_2_data[14]), .f(rom_2_data[13]), .a(rom_2_data[8]), .b(rom_2_data[9]), .e(rom_2_data[12]),
    .d(rom_2_data[11]), .c(rom_2_data[10]), .dp(rom_2_data[15]));
  _7_Segment_Display #(.active("false")) u_7_segment_display_4 (
    .g(rom_2_data[6]), .f(rom_2_data[5]), .a(rom_2_data[0]), .b(rom_2_data[1]), .e(rom_2_data[4]),
    .d(rom_2_data[3]), .c(rom_2_data[2]), .dp(rom_2_data[7]));
  LED led_91 (.in(transistor_4_out));
  LED led_92 (.in(transistor_4_out));
  not not_14 (not_14_out, rom_1_data[7]);
  LED led_93 (.in(rom_1_data[7]));
  xor xor_12 (xor_12_out, register_23_q[1], rom_1_data[5]);
  Adder #(.width(1)) adder_11 (
    .a(xor_10_out), .b(register_22_q[2]), .out(sum[2]), .cin(adder_13_cout), .cout(adder_11_cout));
  xor xor_13 (xor_13_out, sum[2], and_18_out);
  Adder #(.width(1)) adder_12 (
    .a(xor_13_out), .b(in_28[2]), .out(n74245_17_pin2[2]), .cin(adder_14_cout), .cout(adder_12_cout));
  Register register_21 (
    .D(n74245_1_pin18), .en(rom_1_data[13]), .clk(transistor_4_out), .Q(register_21_q), .clr(not_2_out));
  LED led_94 (.in(transistor_4_out));
  Register register_22 (
    .D(n74245_1_pin18), .en(rom_1_data[8]), .clk(transistor_4_out), .Q(register_22_q), .clr(not_2_out));
  Register register_23 (
    .D(n74245_1_pin18), .en(rom_1_data[4]), .clk(transistor_4_out), .Q(register_23_q), .clr(not_2_out));
  LED led_95 (.in(rom_1_data[4]));
  xor xor_14 (xor_14_out, register_23_q[0], rom_1_data[5]);
  Adder #(.width(1)) adder_13 (
    .a(xor_12_out), .b(register_22_q[1]), .out(sum[1]), .cin(adder_15_cout), .cout(adder_13_cout));
  xor xor_15 (xor_15_out, sum[1], and_18_out);
  Adder #(.width(1)) adder_14 (
    .a(xor_15_out), .b(in_28[1]), .out(n74245_17_pin2[1]), .cin(adder_16_cout), .cout(adder_14_cout));
  LED led_96 (.in(register_21_q[7]));
  LED led_97 (.in(register_21_q[6]));
  not not_15 (n74245_21_pin19, C_out);
  not not_16 (not_16_out, B_out);
  LED led_98 (.in(B_out));
  LED led_99 (.in(C_In));
  Adder #(.width(1)) adder_15 (
    .a(xor_14_out), .b(register_22_q[0]), .out(sum[0]), .cin(rom_1_data[5]), .cout(adder_15_cout));
  xor xor_16 (xor_16_out, sum[0], and_18_out);
  Adder #(.width(1)) adder_16 (
    .a(xor_16_out), .b(in_28[0]), .out(n74245_17_pin2[0]), .cin(and_18_out), .cout(adder_16_cout));
  LED led_100 (.in(pull_resistor_8_node[3]));
  LED led_101 (.in(register_21_q[0]));
  LED led_102 (.in(register_21_q[1]));
  LED led_103 (.in(register_21_q[2]));
  LED led_104 (.in(register_21_q[3]));
  LED led_105 (.in(register_21_q[5]));
  LED led_106 (.in(register_21_q[4]));
  LED led_107 (.in(register_22_q[0]));
  LED led_108 (.in(register_22_q[1]));
  LED led_109 (.in(register_22_q[2]));
  LED led_110 (.in(register_22_q[3]));
  LED led_111 (.in(register_22_q[4]));
  LED led_112 (.in(register_22_q[5]));
  LED led_113 (.in(register_22_q[6]));
  LED led_114 (.in(register_22_q[7]));
  LED led_115 (.in(register_23_q[0]));
  LED led_116 (.in(register_23_q[1]));
  LED led_117 (.in(register_23_q[2]));
  LED led_118 (.in(register_23_q[3]));
  LED led_119 (.in(register_23_q[4]));
  LED led_120 (.in(register_23_q[5]));
  LED led_121 (.in(register_23_q[6]));
  LED led_122 (.in(register_23_q[7]));
  LED led_123 (.in(C_out));
  LED led_124 (.in(pull_resistor_8_node[2]));
  LED led_125 (.in(pull_resistor_8_node[1]));
  LED led_126 (.in(pull_resistor_8_node[0]));
  _74245 #(.VccGndPorts("true")) u_74245_22 (
    .pin1(n74245_22_pin1), .pin2(register_21_q[0]), .pin3(register_21_q[1]), .pin4(register_21_q[2]),
    .pin5(register_21_q[3]), .pin6(n74245_22_pin6), .pin7(n74245_22_pin6), .pin8(n74245_22_pin6),
    .pin9(n74245_22_pin6), .pin10(n74245_22_pin6), .pin20(n74245_22_pin1), .pin18(n74245_22_pin18[0]),
    .pin17(n74245_22_pin18[1]), .pin16(n74245_22_pin18[2]), .pin15(n74245_22_pin18[3]));  // open: pin19, pin14, pin13, pin12, pin11
  _74245 #(.VccGndPorts("true")) u_74245_23 (
    .pin1(n74245_23_pin1), .pin2(register_22_q[0]), .pin3(register_22_q[1]), .pin4(register_22_q[2]),
    .pin5(register_22_q[3]), .pin6(register_22_q[4]), .pin7(register_22_q[5]), .pin8(register_22_q[6]),
    .pin9(register_22_q[7]), .pin10(n74245_23_pin10), .pin20(n74245_23_pin1), .pin19(not_14_out),
    .pin18(n74245_1_pin18[0]), .pin17(n74245_1_pin18[1]), .pin16(n74245_1_pin18[2]),
    .pin15(n74245_1_pin18[3]), .pin14(n74245_1_pin18[4]), .pin13(n74245_1_pin18[5]),
    .pin12(n74245_1_pin18[6]), .pin11(n74245_1_pin18[7]));
  _74245 #(.VccGndPorts("true")) u_74245_24 (
    .pin1(n74245_24_pin1), .pin2(register_23_q[0]), .pin3(register_23_q[1]), .pin4(register_23_q[2]),
    .pin5(register_23_q[3]), .pin6(register_23_q[4]), .pin7(register_23_q[5]), .pin8(register_23_q[6]),
    .pin9(register_23_q[7]), .pin10(n74245_24_pin10), .pin20(n74245_24_pin1), .pin19(not_16_out),
    .pin18(n74245_1_pin18[0]), .pin17(n74245_1_pin18[1]), .pin16(n74245_1_pin18[2]),
    .pin15(n74245_1_pin18[3]), .pin14(n74245_1_pin18[4]), .pin13(n74245_1_pin18[5]),
    .pin12(n74245_1_pin18[6]), .pin11(n74245_1_pin18[7]));
  LED led_127 (.in(rom_1_data[2]));
  _74157 #(.ShowInternalStructure("true"), .VccGndPorts("true")) u_74157_1 (
    .pin1(not_7_out), .pin2(AR_Input[0]), .pin3(n74245_22_pin18[0]), .pin4(pull_resistor_8_node[0]),
    .pin5(AR_Input[1]), .pin6(n74245_22_pin18[1]), .pin7(pull_resistor_8_node[1]), .pin8(n74157_1_pin8),
    .pin16(n74157_1_pin16), .pin14(AR_Input[3]), .pin13(n74245_22_pin18[3]), .pin12(pull_resistor_8_node[3]),
    .pin11(AR_Input[2]), .pin10(n74245_22_pin18[2]), .pin9(pull_resistor_8_node[2]));  // open: pin15
  not not_17 (n74245_18_pin19, rom_1_data[1]);
  LED led_128 (.in(rom_1_data[1]));
  not not_18 (n74161_1_pin9, rom_1_data[0]);
  LED led_129 (.in(rom_1_data[0]));
  not not_19 (n74161_1_pin1, not_2_out);
  LED led_130 (.in(not_2_out));
  LED led_131 (.in(not_7_out));
  _7_Segment_Display #(.active("false")) u_7_segment_display_5 (
    .g(not_8_out[6]), .f(1'b1), .a(1'b1), .b(1'b1), .e(1'b1), .d(1'b1), .c(1'b1), .dp(1'b1));
  _7_Segment_Display #(.active("false")) u_7_segment_display_6 (
    .g(rom_2_data[22]), .f(rom_2_data[21]), .a(rom_2_data[16]), .b(rom_2_data[17]), .e(rom_2_data[20]),
    .d(rom_2_data[19]), .c(rom_2_data[18]), .dp(rom_2_data[23]));
  _7_Segment_Display #(.active("false")) u_7_segment_display_7 (
    .g(rom_2_data[14]), .f(rom_2_data[13]), .a(rom_2_data[8]), .b(rom_2_data[9]), .e(rom_2_data[12]),
    .d(rom_2_data[11]), .c(rom_2_data[10]), .dp(rom_2_data[15]));
  Button button_2 ();  // open: out
  _7_Segment_Display #(.active("false")) u_7_segment_display_8 (
    .g(rom_2_data[6]), .f(rom_2_data[5]), .a(rom_2_data[0]), .b(rom_2_data[1]), .e(rom_2_data[4]),
    .d(rom_2_data[3]), .c(rom_2_data[2]), .dp(rom_2_data[7]));
  // also tied to GND on the sheet: {n74163_1_pin8, n74138_1_pin4, n74245_1_pin10, n74245_17_pin10, n74245_18_pin18, n74245_19_pin6, n74245_18_pin1, n74245_21_pin10, n74245_20_pin10, n74161_1_pin8, n74245_23_pin10, n74245_24_pin10, n74245_22_pin6, n74157_1_pin8}
  // also tied to VCC on the sheet: {n74163_1_pin7, n74245_1_pin1, n74138_1_pin6, n74245_17_pin1, n74245_18_pin20, n74245_19_pin1, n74245_21_pin1, n74161_1_pin16, n74245_20_pin1, n74245_23_pin1, n74245_24_pin1, n74245_22_pin1, n74157_1_pin16}

  // Notes on the sheet:
  //   On/Off
  //   Hold
  //   Master Reset
  //   Clock
  //   reset*
  //   Instruction
  //   reset
  //   step
  //   vcc
  //   vcc
  //   vcc
  //   vcc
  //   vcc
  //   vcc
  //   vcc
  //   vcc
  //   vcc
  //   vcc
  //   vcc
  //   vcc
  //   vcc
  //   vcc
  //   vcc
  //   vcc
  //   t0  t1  t2  t3  t4
  //   16 Byte Static RAM
  //   GND
  //   GND
  //   GND
  //   GND
  //   GND
  //   GND
  //   GND
  //   GND
  //   GND
  //   GND
  //   GND
  //   GND
  //   GND
  //   GND
  //   GND
  //   GND
  //   bus
  //   en*
  //   clk
  //   load
  //   bus
  //   clk
  //   load
  //   bus
  //   clk
  //   load
  //   bus
  //   clk
  //   load
  //   bus
  //   clk
  //   load
  //   bus
  //   clk
  //   load
  //   bus
  //   clk
  //   load
  //   bus
  //   clk
  //   load
  //   bus
  //   clk
  //   load
  //   bus
  //   clk
  //   load
  //   bus
  //   clk
  //   load
  //   bus
  //   clk
  //   load
  //   bus
  //   clk
  //   load
  //   bus
  //   clk
  //   load
  //   bus
  //   clk
  //   load
  //   bus
  //   clk
  //   load
  //   load En
  //   out en
  //   bus
  //   add..
  //   contents of rom_1 (hex, n*v repeats v):
  //   2002 a04 6*0 2002 a04 2400 900 4*0 2002 a04 2400 810 140 91*0 2002 a04 88 5*0 2002 a04 4000
  //   RAM Load
  //   RAM out
  //   en*
  //   contents of rom_2 (hex, n*v repeats v):
  //   c0c0c0 c0c0f9 c0c0a4 c0c0b0 c0c099 c0c092 c0c082 c0c0f8 c0c080 c0c090 c0f9c0 c0f9f9 c0f9a4 c0f9b0
  //   c0f999 c0f992 c0f982 c0f9f8 c0f980 c0f990 c0a4c0 c0a4f9 c0a4a4 c0a4b0 c0a499 c0a492 c0a482 c0a4f8
  //   c0a480 c0a490 c0b0c0 c0b0f9 c0b0a4 c0b0b0 c0b099 c0b092 c0b082 c0b0f8 c0b080 c0b090 c099c0 c099f9
  //   c099a4 c099b0 c09999 c09992 c09982 c099f8 c09980 c09990 c092c0 c092f9 c092a4 c092b0 c09299 c09292
  //   c09282 c092f8 c09280 c09290 c082c0 c082f9 c082a4 c082b0 c08299 c08292 c08282 c082f8 c08280 c08290
  //   c0f8c0 c0f8f9 c0f8a4 c0f8b0 c0f899 c0f892 c0f882 c0f8f8 c0f880 c0f890 c080c0 c080f9 c080a4 c080b0
  //   c08099 c08092 c08082 c080f8 c08080 c08090 c090c0 c090f9 c090a4 c090b0 c09099 c09092 c09082 c090f8
  //   c09080 c09090 f9c0c0 f9c0f9 f9c0a4 f9c0b0 f9c099 f9c092 f9c082 f9c0f8 f9c080 f9c090 f9f9c0 f9f9f9
  //   f9f9a4 f9f9b0 f9f999 f9f992 f9f982 f9f9f8 f9f980 f9f990 f9a4c0 f9a4f9 f9a4a4 f9a4b0 f9a499 f9a492
  //   f9a482 f9a4f8 f9a480 f9a490 f9b0c0 f9b0f9 f9b0a4 f9b0b0 f9b099 f9b092 f9b082 f9b0f8 f9b080 f9b090
  //   f999c0 f999f9 f999a4 f999b0 f99999 f99992 f99982 f999f8 f99980 f99990 f992c0 f992f9 f992a4 f992b0
  //   f99299 f99292 f99282 f992f8 f99280 f99290 f982c0 f982f9 f982a4 f982b0 f98299 f98292 f98282 f982f8
  //   f98280 f98290 f9f8c0 f9f8f9 f9f8a4 f9f8b0 f9f899 f9f892 f9f882 f9f8f8 f9f880 f9f890 f980c0 f980f9
  //   f980a4 f980b0 f98099 f98092 f98082 f980f8 f98080 f98090 f990c0 f990f9 f990a4 f990b0 f99099 f99092
  //   f99082 f990f8 f99080 f99090 a4c0c0 a4c0f9 a4c0a4 a4c0b0 a4c099 a4c092 a4c082 a4c0f8 a4c080 a4c090
  //   a4f9c0 a4f9f9 a4f9a4 a4f9b0 a4f999 a4f992 a4f982 a4f9f8 a4f980 a4f990 a4a4c0 a4a4f9 a4a4a4 a4a4b0
  //   a4a499 a4a492 a4a482 a4a4f8 a4a480 a4a490 a4b0c0 a4b0f9 a4b0a4 a4b0b0 a4b099 a4b092 a4b082 a4b0f8
  //   a4b080 a4b090 a499c0 a499f9 a499a4 a499b0 a49999 a49992 a49982 a499f8 a49980 a49990 a492c0 a492f9
  //   a492a4 a492b0 a49299 a49292
  //   ROM For Disp
  //   Bus
  //   Address
  //   Data
  //   On/Off
  //   Hold
  //   Clock
  //   ALU
  //   En*
  //   OUTPUT Register
  //   load
  //   clr
  //   enable*
  //   load
  //   clr
  //   enable*
  //   load
  //   clr
  //   enable*
  //   1 => negetive
  //   enable disp
  //   S/out
  //   A
  //   B
  //   A
  //   Program Counter
  //   Control Unit
  //   in 2S
  //   OR
  //   IR
  //   sing
  //   Chache Memory
  //   Main
  //   C
  //   8 bit Adder / Subtractor
  //   count en
  //   count out*
  //   Load*
  //   load
  //   clr
  //   load
  //   clr
  //   enable*
  //   load
  //   clr
  //   enable*
  //   result
  //   sum
  //   A in
  //   B in
  //   0->(+)
  //   ctr
  //   __  HD  MI  RI  RO  IO  II AI  AO  {O  SU  BI  OI  CE  CO  J
  //   AR
  //   Memory Address Resister
  //   A
  //   A out
  //   B
  //   B out
  //   addres
  //   0->in / 1-> AR
  //   Clock Hold
  //   Clear All
endmodule
