// Logisim project A_to_B_data_load.circ as structural Verilog: 1 circuit, main circuit main
module main (
  input  A,
  input  B,
  input  [7:0] in_3,
  input  M,
  output [7:0] out_5,
  output [7:0] out_6
);

  wire clock_1_out;
  wire [7:0] register_2_q;

  Register register_1 (.D(register_2_q), .en(A), .clk(clock_1_out), .Q(out_5));  // open: clr
  Register register_2 (.D(in_3), .en(M), .clk(clock_1_out), .Q(register_2_q));  // open: clr
  Register register_3 (.D(register_2_q), .en(B), .clk(clock_1_out), .Q(out_6));  // open: clr
  Clock clock_1 (.out(clock_1_out));

  // Notes on the sheet:
  //   A
  //   Bus System A to B
  //   M
  //   B
endmodule
