// Logisim project complete_register_bus_system.circ as structural Verilog: 1 circuit, main circuit main
module main (
  input  [7:0] in_1,
  input  load,
  input  load_2,
  input  enable_star,
  input  enable_star_2,
  input  load_3,
  input  load_4,
  input  enable_star_3,
  input  enable_star_4
);

  wire button_1_out, button_2_out, button_3_out, button_4_out, clock_1_out, clock_2_out, clock_3_out,
       clock_4_out, n74245_1_pin1, n74245_1_pin10, n74245_2_pin1, n74245_2_pin10, n74245_3_pin1,
       n74245_3_pin10, n74245_4_pin1, n74245_4_pin10;
  wire [7:0] n74245_1_pin18, register_1_q, register_2_q, register_3_q, register_4_q;

  Register register_1 (.D(in_1), .en(load_2), .clk(clock_1_out), .Q(register_1_q), .clr(button_1_out));
  Clock clock_1 (.out(clock_1_out));
  LED led_1 (.in(clock_1_out));
  Button button_1 (.out(button_1_out));
  Register register_2 (.D(n74245_1_pin18), .en(load_4), .clk(clock_2_out), .Q(register_2_q), .clr(button_2_out));
  Clock clock_2 (.out(clock_2_out));
  LED led_2 (.in(clock_2_out));
  Button button_2 (.out(button_2_out));
  LED led_3 (.in(register_1_q[0]));
  LED led_4 (.in(register_1_q[1]));
  LED led_5 (.in(register_1_q[2]));
  LED led_6 (.in(register_1_q[3]));
  LED led_7 (.in(register_1_q[4]));
  LED led_8 (.in(register_1_q[5]));
  LED led_9 (.in(register_1_q[6]));
  LED led_10 (.in(register_1_q[7]));
  LED led_11 (.in(register_2_q[0]));
  LED led_12 (.in(register_2_q[1]));
  LED led_13 (.in(register_2_q[2]));
  LED led_14 (.in(register_2_q[3]));
  LED led_15 (.in(register_2_q[4]));
  LED led_16 (.in(register_2_q[5]));
  LED led_17 (.in(register_2_q[6]));
  LED led_18 (.in(register_2_q[7]));
  _74245 #(.VccGndPorts("true")) u_74245_1 (
    .pin1(n74245_1_pin1), .pin2(register_1_q[0]), .pin3(register_1_q[1]), .pin4(register_1_q[2]),
    .pin5(register_1_q[3]), .pin6(register_1_q[4]), .pin7(register_1_q[5]), .pin8(register_1_q[6]),
    .pin9(register_1_q[7]), .pin10(n74245_1_pin10), .pin20(n74245_1_pin1), .pin19(enable_star_2),
    .pin18(n74245_1_pin18[0]), .pin17(n74245_1_pin18[1]), .pin16(n74245_1_pin18[2]),
    .pin15(n74245_1_pin18[3]), .pin14(n74245_1_pin18[4]), .pin13(n74245_1_pin18[5]),
    .pin12(n74245_1_pin18[6]), .pin11(n74245_1_pin18[7]));
  _74245 #(.VccGndPorts("true")) u_74245_2 (
    .pin1(n74245_2_pin1), .pin2(register_2_q[0]), .pin3(register_2_q[1]), .pin4(register_2_q[2]),
    .pin5(register_2_q[3]), .pin6(register_2_q[4]), .pin7(register_2_q[5]), .pin8(register_2_q[6]),
    .pin9(register_2_q[7]), .pin10(n74245_2_pin10), .pin20(n74245_2_pin1), .pin19(enable_star_4),
    .pin18(n74245_1_pin18[0]), .pin17(n74245_1_pin18[1]), .pin16(n74245_1_pin18[2]),
    .pin15(n74245_1_pin18[3]), .pin14(n74245_1_pin18[4]), .pin13(n74245_1_pin18[5]),
    .pin12(n74245_1_pin18[6]), .pin11(n74245_1_pin18[7]));
  LED led_19 (.in(n74245_1_pin18[7]));
  LED led_20 (.in(n74245_1_pin18[6]));
  LED led_21 (.in(n74245_1_pin18[5]));
  LED led_22 (.in(n74245_1_pin18[4]));
  LED led_23 (.in(n74245_1_pin18[3]));
  LED led_24 (.in(n74245_1_pin18[2]));
  LED led_25 (.in(n74245_1_pin18[1]));
  LED led_26 (.in(n74245_1_pin18[0]));
  Clock clock_3 (.out(clock_3_out));
  Button button_3 (.out(button_3_out));
  Clock clock_4 (.out(clock_4_out));
  Button button_4 (.out(button_4_out));
  Register register_3 (.D(n74245_1_pin18), .en(load), .clk(clock_3_out), .Q(register_3_q), .clr(button_3_out));
  LED led_27 (.in(clock_3_out));
  Register register_4 (.D(n74245_1_pin18), .en(load_3), .clk(clock_4_out), .Q(register_4_q), .clr(button_4_out));
  LED led_28 (.in(clock_4_out));
  LED led_29 (.in(register_3_q[0]));
  LED led_30 (.in(register_3_q[1]));
  LED led_31 (.in(register_3_q[2]));
  LED led_32 (.in(register_3_q[3]));
  LED led_33 (.in(register_3_q[4]));
  LED led_34 (.in(register_3_q[5]));
  LED led_35 (.in(register_3_q[6]));
  LED led_36 (.in(register_3_q[7]));
  LED led_37 (.in(register_4_q[0]));
  LED led_38 (.in(register_4_q[1]));
  LED led_39 (.in(register_4_q[2]));
  LED led_40 (.in(register_4_q[3]));
  LED led_41 (.in(register_4_q[4]));
  LED led_42 (.in(register_4_q[5]));
  LED led_43 (.in(register_4_q[6]));
  LED led_44 (.in(register_4_q[7]));
  _74245 #(.VccGndPorts("true")) u_74245_3 (
    .pin1(n74245_3_pin1), .pin2(register_3_q[0]), .pin3(register_3_q[1]), .pin4(register_3_q[2]),
    .pin5(register_3_q[3]), .pin6(register_3_q[4]), .pin7(register_3_q[5]), .pin8(register_3_q[6]),
    .pin9(register_3_q[7]), .pin10(n74245_3_pin10), .pin20(n74245_3_pin1), .pin19(enable_star),
    .pin18(n74245_1_pin18[0]), .pin17(n74245_1_pin18[1]), .pin16(n74245_1_pin18[2]),
    .pin15(n74245_1_pin18[3]), .pin14(n74245_1_pin18[4]), .pin13(n74245_1_pin18[5]),
    .pin12(n74245_1_pin18[6]), .pin11(n74245_1_pin18[7]));
  _74245 #(.VccGndPorts("true")) u_74245_4 (
    .pin1(n74245_4_pin1), .pin2(register_4_q[0]), .pin3(register_4_q[1]), .pin4(register_4_q[2]),
    .pin5(register_4_q[3]), .pin6(register_4_q[4]), .pin7(register_4_q[5]), .pin8(register_4_q[6]),
    .pin9(register_4_q[7]), .pin10(n74245_4_pin10), .pin20(n74245_4_pin1), .pin19(enable_star_3),
    .pin18(n74245_1_pin18[0]), .pin17(n74245_1_pin18[1]), .pin16(n74245_1_pin18[2]),
    .pin15(n74245_1_pin18[3]), .pin14(n74245_1_pin18[4]), .pin13(n74245_1_pin18[5]),
    .pin12(n74245_1_pin18[6]), .pin11(n74245_1_pin18[7]));
  // also tied to GND on the sheet: {n74245_1_pin10, n74245_2_pin10, n74245_3_pin10, n74245_4_pin10}
  // also tied to VCC on the sheet: {n74245_1_pin1, n74245_2_pin1, n74245_3_pin1, n74245_4_pin1}

  // Notes on the sheet:
  //   clr
  //   clr
  //   Bus
  //   M
  //   B
  //   clr
  //   clr
  //   A
  //   C
endmodule
