// Logisim project 3Digit_7segment_with_3rom_disp.circ as structural Verilog: 1 circuit, main circuit main
module main (
  input  [3:0] in_1,
  input  [3:0] in_2,
  input  [3:0] in_3
);

  wire [3:0] rom_1_data, rom_1_data_2, rom_2_data, rom_2_data_2, rom_3_data, rom_3_data_2;

  _7_Segment_Display #(.active("false")) u_7_segment_display_1 (
    .g(rom_1_data_2[3]), .f(rom_1_data_2[2]), .a(rom_1_data_2[1]), .b(rom_1_data_2[0]), .e(rom_1_data[3]),
    .d(rom_1_data[2]), .c(rom_1_data[1]), .dp(rom_1_data[0]));
  _7_Segment_Display #(.active("false")) u_7_segment_display_2 (
    .g(rom_2_data_2[3]), .f(rom_2_data_2[2]), .a(rom_2_data_2[1]), .b(rom_2_data_2[0]), .e(rom_2_data[3]),
    .d(rom_2_data[2]), .c(rom_2_data[1]), .dp(rom_2_data[0]));
  _7_Segment_Display #(.active("false")) u_7_segment_display_3 (
    .g(rom_3_data_2[3]), .f(rom_3_data_2[2]), .a(rom_3_data_2[1]), .b(rom_3_data_2[0]), .e(rom_3_data[3]),
    .d(rom_3_data[2]), .c(rom_3_data[1]), .dp(rom_3_data[0]));
  ROM #(.addrWidth(4)) rom_1 (
    .addr(in_1), .data({rom_1_data[0], rom_1_data_2[3:2], rom_1_data[3:1], rom_1_data_2[0], rom_1_data_2[1]}));
  ROM #(.addrWidth(4)) rom_2 (
    .addr(in_2), .data({rom_2_data[0], rom_2_data_2[3:2], rom_2_data[3:1], rom_2_data_2[0], rom_2_data_2[1]}));
  ROM #(.addrWidth(4)) rom_3 (
    .addr(in_3), .data({rom_3_data[0], rom_3_data_2[3:2], rom_3_data[3:1], rom_3_data_2[0], rom_3_data_2[1]}));

  // Notes on the sheet:
  //   #3 Digit decimal Display
  //   contents of rom_1 (hex, n*v repeats v):
  //   c0 f9 a4 b0 99 92 82 f8 80 90 88 83 c6 a1 86 8e
  //   contents of rom_2 (hex, n*v repeats v):
  //   c0 f9 a4 b0 99 92 82 f8 80 90 88 83 c6 a1 86 8e
  //   contents of rom_3 (hex, n*v repeats v):
  //   c0 f9 a4 b0 99 92 82 f8 80 90 88 83 c6 a1 86 8e
endmodule
