// Logisim project JK.circ as structural Verilog: 1 circuit, main circuit main
module main (
  input  in_1,
  input  in_2,
  output Q,
  output Q_star,
  output out_5
);

  wire and_1_out, and_2_out, and_3_out, and_4_out, button_1_out, button_2_out, button_3_out, d_ff_1_qn,
       digital_oscilloscope_1_p1, or_1_out;

  Button button_1 (.out(button_1_out));
  Button button_2 (.out(button_2_out));
  Button button_3 (.out(button_3_out));
  and and_1 (and_1_out, Q_star, button_1_out, button_2_out);
  and and_2 (and_2_out, button_2_out, button_3_out, Q);
  and and_3 (and_3_out, in_1, d_ff_1_qn);
  and and_4 (and_4_out, out_5, in_2);
  // Digital_Oscilloscope digital_oscilloscope_1: pin names not known; wires that end beside it: digital_oscilloscope_1_p1, out_5, in_2, in_1
  or or_1 (or_1_out, and_3_out, and_4_out);
  nor nor_1 (Q, and_1_out, Q_star);
  nor nor_2 (Q_star, Q, and_2_out);
  D_Flip_Flop d_ff_1 (.D(or_1_out), .clk(digital_oscilloscope_1_p1), .Q(out_5), .Qn(d_ff_1_qn));  // open: preset, reset
  Clock clock_1 (.out(digital_oscilloscope_1_p1));
  LED led_1 (.in(Q));
  LED led_2 (.in(Q_star));

  // Notes on the sheet:
  //   K
  //   clk
  //   J
  //   JK FlipFlop with Racing Problem
endmodule
