// Logisim project Jk_master_preset_clear.circ as structural Verilog: 1 circuit, main circuit main
module main (
  output Q,
  output Q_star
);

  wire button_1_out, button_2_out, button_3_out, button_4_out, clock_1_out, nand_1_out, nand_2_out,
       nand_3_out, nand_4_out, nand_5_out, nand_6_out, not_1_out, not_2_out, not_3_out;

  Button button_1 (.out(button_1_out));
  Button button_2 (.out(button_2_out));
  Clock clock_1 (.out(clock_1_out));
  Button button_3 (.out(button_3_out));
  Button button_4 (.out(button_4_out));
  not not_1 (not_1_out, button_1_out);
  nand nand_1 (nand_1_out, Q_star, button_2_out, clock_1_out);
  nand nand_2 (nand_2_out, clock_1_out, button_3_out, Q);
  not not_2 (not_2_out, button_4_out);
  nand nand_3 (nand_3_out, not_1_out, nand_1_out, nand_4_out);
  nand nand_4 (nand_4_out, nand_3_out, nand_2_out, not_2_out);
  not not_3 (not_3_out, clock_1_out);
  nand nand_5 (nand_5_out, nand_3_out, not_3_out);
  nand nand_6 (nand_6_out, not_3_out, nand_4_out);
  nand nand_7 (Q, nand_5_out, Q_star);
  nand nand_8 (Q_star, Q, nand_6_out);
  LED led_1 (.in(Q));
  LED led_2 (.in(Q_star));

  // Notes on the sheet:
  //   preset
  //   J
  //   clk
  //   K
  //   clear
  //   Jk master slave with preset clear
endmodule
