// Logisim project Master_Slave_JK.circ as structural Verilog: 1 circuit, main circuit main
module main (
  input  J,
  input  K,
  output Q,
  output Q_star
);

  wire and_1_out, and_2_out, and_3_out, and_4_out, clock_1_out, nor_1_out, nor_2_out, not_1_out;

  Clock clock_1 (.out(clock_1_out));
  and and_1 (and_1_out, Q_star, J, clock_1_out);
  and and_2 (and_2_out, clock_1_out, K, Q);
  nor nor_1 (nor_1_out, and_1_out, nor_2_out);
  LED led_1 (.in(nor_1_out));
  nor nor_2 (nor_2_out, nor_1_out, and_2_out);
  LED led_2 (.in(nor_2_out));
  not not_1 (not_1_out, clock_1_out);
  and and_3 (and_3_out, nor_1_out, not_1_out);
  and and_4 (and_4_out, not_1_out, nor_2_out);
  nor nor_3 (Q, and_3_out, Q_star);
  nor nor_4 (Q_star, Q, and_4_out);
  LED led_3 (.in(Q));
  LED led_4 (.in(Q_star));

  // Notes on the sheet:
  //   clk
  //   Master-Slave  JK Flipflop
  //   S
  //   R
  //   clk 1 active
  //   Q*
  //   Q
  //   R
  //   S
  //   clk 0 active
endmodule
