// Logisim project D.circ as structural Verilog: 1 circuit, main circuit main
module main (
  output Q,
  output Q_star
);

  wire and_1_out, and_2_out, button_1_out, button_2_out, not_1_out;

  LED led_1 (.in(button_1_out));
  Button button_1 (.out(button_1_out));
  LED led_2 (.in(button_2_out));
  Button button_2 (.out(button_2_out));
  not not_1 (not_1_out, button_2_out);
  and and_1 (and_1_out, not_1_out, button_1_out);
  and and_2 (and_2_out, button_1_out, button_2_out);
  nor nor_1 (Q, and_1_out, Q_star);
  nor nor_2 (Q_star, Q, and_2_out);
  LED led_3 (.in(Q));
  LED led_4 (.in(Q_star));

  // Notes on the sheet:
  //   D Latch
  //   EN
  //   D
endmodule
