// Logisim project SR.circ as structural Verilog: 1 circuit, main circuit main
module main (
  output Q,
  output Q_star
);

  wire button_1_out, button_2_out;

  LED led_1 (.in(button_1_out));
  Button button_1 (.out(button_1_out));
  LED led_2 (.in(button_2_out));
  Button button_2 (.out(button_2_out));
  nor nor_1 (Q, button_1_out, Q_star);
  nor nor_2 (Q_star, Q, button_2_out);
  LED led_3 (.in(Q));
  LED led_4 (.in(Q_star));

  // Notes on the sheet:
  //   SR Latch
  //   R
  //   S
endmodule
