// Logisim project SR_EN.circ as structural Verilog: 1 circuit, main circuit main
module main (
  output Q,
  output Q_star
);

  wire and_1_out, and_2_out, button_1_out, button_2_out, switch_1_p2;

  LED led_1 (.in(button_1_out));
  Button button_1 (.out(button_1_out));
  LED led_2 (.in(switch_1_p2));
  // Switch switch_1: pin names not known; wires that end beside it: 1'b1, switch_1_p2
  LED led_3 (.in(button_2_out));
  Button button_2 (.out(button_2_out));
  and and_1 (and_1_out, button_1_out, switch_1_p2);
  and and_2 (and_2_out, switch_1_p2, button_2_out);
  nor nor_1 (Q, and_1_out, Q_star);
  nor nor_2 (Q_star, Q, and_2_out);
  LED led_4 (.in(Q));
  LED led_5 (.in(Q_star));

  // Notes on the sheet:
  //   SR Latch
  //   R
  //   EN
  //   S
endmodule
