// Logisim project 1bit_HalfAdder.circ as structural Verilog: 1 circuit, main circuit main
module main (
  input  A,
  input  B,
  output Sum,
  output carry
);

  and and_1 (carry, A, B);
  xor xor_1 (Sum, A, B);

  // Notes on the sheet:
  //   Half Adder
endmodule
