// Logisim project 1x8_De_Multiplexer.circ as structural Verilog: 1 circuit, main circuit main
module main (
  input  C,
  input  in_2,
  input  in_3
);

  wire and_1_out, and_2_out, and_3_out, and_4_out, and_5_out, and_6_out, and_7_out, and_8_out, button_1_out,
       not_1_out, not_2_out, not_3_out;

  Button button_1 (.out(button_1_out));
  not not_1 (not_1_out, C);
  not not_2 (not_2_out, in_2);
  not not_3 (not_3_out, in_3);
  and and_1 (and_1_out, button_1_out, not_3_out, not_2_out, not_1_out);
  and and_2 (and_2_out, button_1_out, in_3, not_2_out, not_1_out);
  and and_3 (and_3_out, button_1_out, not_3_out, in_2, not_1_out);
  and and_4 (and_4_out, button_1_out, in_3, in_2, not_1_out);
  and and_5 (and_5_out, button_1_out, not_3_out, not_2_out, C);
  and and_6 (and_6_out, button_1_out, in_3, not_2_out, C);
  and and_7 (and_7_out, button_1_out, not_3_out, in_2, C);
  and and_8 (and_8_out, button_1_out, in_3, in_2, C);
  LED led_1 (.in(and_1_out));
  LED led_2 (.in(and_2_out));
  LED led_3 (.in(and_3_out));
  LED led_4 (.in(and_4_out));
  LED led_5 (.in(and_5_out));
  LED led_6 (.in(and_6_out));
  LED led_7 (.in(and_7_out));
  LED led_8 (.in(and_8_out));

  // Notes on the sheet:
  //   8 x 1 DE-Multiplexer
  //   in
  //   B
  //   A
  //   D0
  //   D1
  //   D2
  //   D3
  //   D4
  //   D5
  //   D6
  //   D7
endmodule
