// Logisim project 4x1_Mul.circ as structural Verilog: 1 circuit, main circuit main
module main (
  input  B,
  input  in_2,
  output out_3
);

  wire and_1_out, and_2_out, and_3_out, and_4_out, button_1_out, button_2_out, button_3_out, button_4_out,
       not_1_out, not_2_out;

  Button button_1 (.out(button_1_out));
  Button button_2 (.out(button_2_out));
  Button button_3 (.out(button_3_out));
  Button button_4 (.out(button_4_out));
  not not_1 (not_1_out, B);
  not not_2 (not_2_out, in_2);
  and and_1 (and_1_out, button_1_out, not_2_out, not_1_out);
  and and_2 (and_2_out, button_2_out, in_2, not_1_out);
  and and_3 (and_3_out, button_3_out, B, not_2_out);
  and and_4 (and_4_out, button_4_out, B, in_2);
  or or_1 (out_3, and_1_out, and_2_out, and_3_out, and_4_out);
  LED led_1 (.in(out_3));

  // Notes on the sheet:
  //   4 x 1 Multiplexer
  //   D0
  //   D1
  //   D2
  //   D3
  //   A
endmodule
