// Logisim project 7segment_decoder_4bit.circ as structural Verilog: 1 circuit, main circuit main
module main (
);

  wire and_1_out, and_2_out, and_3_out, and_4_out, and_5_out, and_6_out, and_7_out, and_8_out, and_9_out,
       and_10_out, and_11_out, and_12_out, and_13_out, and_14_out, and_15_out, and_16_out, not_1_out,
       not_2_out, not_3_out, not_4_out, or_1_out, or_2_out, or_3_out, or_4_out, or_5_out, or_6_out, or_7_out;
  wire [3:0] undriven;

  not not_1 (not_1_out, undriven[3]);
  not not_2 (not_2_out, undriven[0]);
  not not_3 (not_3_out, undriven[1]);
  not not_4 (not_4_out, undriven[2]);
  and and_1 (and_1_out, not_4_out, not_2_out);
  and and_2 (and_2_out, undriven[2], undriven[0]);
  and and_3 (and_3_out, not_3_out, not_2_out);
  and and_4 (and_4_out, undriven[1], undriven[0]);
  and and_5 (and_5_out, not_4_out, not_2_out);
  and and_6 (and_6_out, not_4_out, undriven[1]);
  and and_7 (and_7_out, undriven[2], not_3_out, undriven[0]);
  and and_8 (and_8_out, not_4_out, not_2_out);
  and and_9 (and_9_out, undriven[1], not_2_out);
  and and_10 (and_10_out, not_3_out, not_2_out);
  and and_11 (and_11_out, undriven[2], not_3_out);
  and and_12 (and_12_out, undriven[2], not_2_out);
  and and_13 (and_13_out, not_4_out, undriven[1]);
  and and_14 (and_14_out, undriven[2], not_3_out);
  and and_15 (and_15_out, undriven[2], not_2_out);
  or or_1 (or_1_out, not_3_out, undriven[0], undriven[2]);
  and and_16 (and_16_out, undriven[1], not_2_out);
  or or_2 (or_2_out, and_8_out, and_9_out);
  or or_3 (or_3_out, undriven[1], and_1_out, and_2_out, undriven[3]);
  or or_4 (or_4_out, not_4_out, and_3_out, and_4_out);
  or or_5 (or_5_out, and_6_out, and_7_out, undriven[3], and_5_out, and_16_out);
  or or_6 (or_6_out, and_10_out, and_11_out, and_12_out, undriven[3]);
  or or_7 (or_7_out, and_13_out, and_14_out, undriven[3], and_15_out);
  _7_Segment_Display u_7_segment_display_1 (
    .g(or_7_out), .f(or_6_out), .a(or_3_out), .b(or_4_out), .e(or_2_out), .d(or_5_out), .c(or_1_out));  // open: dp

  // Notes on the sheet:
  //   D
  //   C
  //   B
  //   A
  //   7 segment display
  //   a
  //   b
  //   c
  //   d
  //   e
  //   f
  //   g
  //   B*D* + C + BD + A
  //   B* + C*D* + CD
  //   C* + B + D
  //   B*D*+CD*
  //   C*D*+BC*+BD*+A
  //   B*C+BC*+A+BD*
  //   B*D*+B*C+BC*D+CD*+A
endmodule
