// Logisim project 7segment_decoder_with_IC.circ as structural Verilog: 1 circuit, main circuit main
module main (
);

  wire n7400_1_pin3, n7400_1_pin6, n7400_1_pin8, n7400_1_pin11, n7408_1_pin3, n7408_1_pin6, n7408_1_pin8,
       n7408_1_pin11, n7408_2_pin3, n7408_2_pin6, n7411_1_pin6, n7411_1_pin8, n7411_1_pin12, n7432_1_pin3,
       n7432_1_pin8, n7432_1_pin11, n7432_2_pin2, n7432_2_pin3, n7432_2_pin11, n7432_3_pin3, n7432_3_pin6,
       n7432_4_pin3, n7432_5_pin3, n7432_5_pin6;
  wire [3:0] n7400_1_pin13;
  wire [6:0] n7432_4_pin11;

  _7400 #(.ShowInternalStructure("true")) u_7400_1 (
    .pin1(n7400_1_pin13[2]), .pin2(n7400_1_pin13[2]), .pin3(n7400_1_pin3), .pin4(n7400_1_pin13[3]),
    .pin5(n7400_1_pin13[3]), .pin6(n7400_1_pin6), .pin13(n7400_1_pin13[0]), .pin12(n7400_1_pin13[0]),
    .pin11(n7400_1_pin11), .pin10(n7400_1_pin13[1]), .pin9(n7400_1_pin13[1]), .pin8(n7400_1_pin8));
  _7408 #(.ShowInternalStructure("true")) u_7408_1 (
    .pin1(n7400_1_pin8), .pin2(n7400_1_pin11), .pin3(n7408_1_pin3), .pin4(n7400_1_pin13[0]),
    .pin5(n7400_1_pin13[1]), .pin6(n7408_1_pin6), .pin13(n7400_1_pin3), .pin12(n7400_1_pin11),
    .pin11(n7408_1_pin11), .pin10(n7400_1_pin13[2]), .pin9(n7400_1_pin13[0]), .pin8(n7408_1_pin8));
  _7411 #(.ShowInternalStructure("true")) u_7411_1 (
    .pin1(n7400_1_pin8), .pin2(n7400_1_pin13[0]), .pin3(n7400_1_pin13[1]), .pin4(n7400_1_pin11),
    .pin5(n7400_1_pin11), .pin6(n7411_1_pin6), .pin13(n7400_1_pin13[2]), .pin12(n7411_1_pin12),
    .pin11(n7400_1_pin3), .pin10(n7400_1_pin13[1]), .pin9(n7400_1_pin13[1]), .pin8(n7411_1_pin8));
  _7408 #(.ShowInternalStructure("true")) u_7408_2 (
    .pin1(n7400_1_pin13[2]), .pin2(n7400_1_pin8), .pin3(n7408_2_pin3), .pin4(n7400_1_pin13[2]),
    .pin5(n7400_1_pin11), .pin6(n7408_2_pin6));  // open: pin13, pin12, pin11, pin10, pin9, pin8
  _7432 #(.ShowInternalStructure("true")) u_7432_1 (
    .pin1(n7400_1_pin3), .pin2(n7408_1_pin3), .pin3(n7432_1_pin3), .pin4(n7432_1_pin3), .pin5(n7408_1_pin6),
    .pin6(n7432_4_pin11[1]), .pin13(n7408_1_pin8), .pin12(n7408_1_pin11), .pin11(n7432_1_pin11),
    .pin10(n7400_1_pin13[1]), .pin9(n7400_1_pin13[3]), .pin8(n7432_1_pin8));
  _7432 #(.ShowInternalStructure("true")) u_7432_2 (
    .pin1(n7411_1_pin6), .pin2(n7432_2_pin2), .pin3(n7432_2_pin3), .pin4(n7432_2_pin3),
    .pin5(n7400_1_pin13[3]), .pin6(n7432_4_pin11[3]), .pin13(n7411_1_pin12), .pin12(n7408_1_pin11),
    .pin11(n7432_2_pin11), .pin10(n7432_2_pin11), .pin9(n7411_1_pin8), .pin8(n7432_2_pin2));
  _7432 #(.ShowInternalStructure("true")) u_7432_3 (
    .pin1(n7408_1_pin3), .pin2(n7408_2_pin3), .pin3(n7432_3_pin3), .pin4(n7432_3_pin3), .pin5(n7408_2_pin6),
    .pin6(n7432_3_pin6), .pin13(n7432_3_pin6), .pin12(n7400_1_pin13[3]), .pin11(n7432_4_pin11[5]));  // open: pin10, pin9, pin8
  _7432 #(.ShowInternalStructure("true")) u_7432_4 (
    .pin1(n7400_1_pin8), .pin2(n7400_1_pin13[2]), .pin3(n7432_4_pin3), .pin4(n7432_4_pin3),
    .pin5(n7400_1_pin13[0]), .pin6(n7432_4_pin11[2]), .pin13(n7432_1_pin11), .pin12(n7432_1_pin8),
    .pin11(n7432_4_pin11[0]));  // open: pin10, pin9, pin8
  _7432 #(.ShowInternalStructure("true")) u_7432_5 (
    .pin1(n7411_1_pin8), .pin2(n7408_2_pin3), .pin3(n7432_5_pin3), .pin4(n7432_5_pin3), .pin5(n7408_2_pin6),
    .pin6(n7432_5_pin6), .pin13(n7408_1_pin11), .pin12(n7411_1_pin6), .pin11(n7432_4_pin11[4]),
    .pin10(n7432_5_pin6), .pin9(n7400_1_pin13[3]), .pin8(n7432_4_pin11[6]));

  // Notes on the sheet:
  //   D
  //   C
  //   B
  //   A
  //   display con
  //   binary
  //   7 Segment Display with Decoder
  //   B*D*
  //   b
  //   d
  //   C*D*
  //   B*C
  //   BC*
  //   f
  //   a
  //   CD*
  //   e
  //   c
  //   g
endmodule
