// Logisim project 8bit_adder_sub_with_2s_management.circ as structural Verilog: 1 circuit, main circuit main
module main (
  input  ctr,
  input  [7:0] in_2,
  input  [7:0] in_3,
  input  [7:0] in_4,
  output c_out,
  output [7:0] sum,
  output out_7,
  output [7:0] sum_2
);

  wire adder_3_cout, adder_4_cout, adder_5_cout, adder_6_cout, adder_7_cout, adder_8_cout, adder_9_cout,
       adder_10_cout, adder_11_cout, adder_12_cout, adder_13_cout, adder_14_cout, adder_15_cout,
       adder_16_cout, and_1_out, not_1_out, xor_1_out, xor_2_out, xor_3_out, xor_4_out, xor_5_out, xor_6_out,
       xor_7_out, xor_8_out, xor_9_out, xor_10_out, xor_11_out, xor_12_out, xor_13_out, xor_14_out,
       xor_15_out, xor_16_out;

  xor xor_1 (xor_1_out, in_3[7], ctr);
  xor xor_2 (xor_2_out, sum[7], and_1_out);
  xor xor_3 (xor_3_out, in_3[6], ctr);
  Adder #(.width(1)) adder_1 (.a(xor_1_out), .b(in_2[7]), .out(sum[7]), .cin(adder_3_cout), .cout(c_out));
  not not_1 (not_1_out, c_out);
  and and_1 (and_1_out, not_1_out, ctr);
  LED led_1 (.in(and_1_out));
  xor xor_4 (xor_4_out, sum[6], and_1_out);
  Adder #(.width(1)) adder_2 (.a(xor_2_out), .b(in_4[7]), .out(sum_2[7]), .cin(adder_4_cout), .cout(out_7));
  xor xor_5 (xor_5_out, in_3[5], ctr);
  Adder #(.width(1)) adder_3 (.a(xor_3_out), .b(in_2[6]), .out(sum[6]), .cin(adder_5_cout), .cout(adder_3_cout));
  xor xor_6 (xor_6_out, sum[5], and_1_out);
  Adder #(.width(1)) adder_4 (.a(xor_4_out), .b(in_4[6]), .out(sum_2[6]), .cin(adder_6_cout), .cout(adder_4_cout));
  xor xor_7 (xor_7_out, in_3[4], ctr);
  Adder #(.width(1)) adder_5 (.a(xor_5_out), .b(in_2[5]), .out(sum[5]), .cin(adder_7_cout), .cout(adder_5_cout));
  xor xor_8 (xor_8_out, sum[4], and_1_out);
  Adder #(.width(1)) adder_6 (.a(xor_6_out), .b(in_4[5]), .out(sum_2[5]), .cin(adder_8_cout), .cout(adder_6_cout));
  xor xor_9 (xor_9_out, in_3[3], ctr);
  Adder #(.width(1)) adder_7 (.a(xor_7_out), .b(in_2[4]), .out(sum[4]), .cin(adder_9_cout), .cout(adder_7_cout));
  xor xor_10 (xor_10_out, sum[3], and_1_out);
  Adder #(.width(1)) adder_8 (.a(xor_8_out), .b(in_4[4]), .out(sum_2[4]), .cin(adder_10_cout), .cout(adder_8_cout));
  xor xor_11 (xor_11_out, in_3[2], ctr);
  Adder #(.width(1)) adder_9 (.a(xor_9_out), .b(in_2[3]), .out(sum[3]), .cin(adder_11_cout), .cout(adder_9_cout));
  xor xor_12 (xor_12_out, sum[2], and_1_out);
  Adder #(.width(1)) adder_10 (.a(xor_10_out), .b(in_4[3]), .out(sum_2[3]), .cin(adder_12_cout), .cout(adder_10_cout));
  xor xor_13 (xor_13_out, in_3[1], ctr);
  Adder #(.width(1)) adder_11 (.a(xor_11_out), .b(in_2[2]), .out(sum[2]), .cin(adder_13_cout), .cout(adder_11_cout));
  xor xor_14 (xor_14_out, sum[1], and_1_out);
  Adder #(.width(1)) adder_12 (.a(xor_12_out), .b(in_4[2]), .out(sum_2[2]), .cin(adder_14_cout), .cout(adder_12_cout));
  xor xor_15 (xor_15_out, in_3[0], ctr);
  Adder #(.width(1)) adder_13 (.a(xor_13_out), .b(in_2[1]), .out(sum[1]), .cin(adder_15_cout), .cout(adder_13_cout));
  xor xor_16 (xor_16_out, sum[0], and_1_out);
  Adder #(.width(1)) adder_14 (.a(xor_14_out), .b(in_4[1]), .out(sum_2[1]), .cin(adder_16_cout), .cout(adder_14_cout));
  Adder #(.width(1)) adder_15 (.a(xor_15_out), .b(in_2[0]), .out(sum[0]), .cin(ctr), .cout(adder_15_cout));
  Adder #(.width(1)) adder_16 (.a(xor_16_out), .b(in_4[0]), .out(sum_2[0]), .cin(and_1_out), .cout(adder_16_cout));

  // Notes on the sheet:
  //   A
  //   B
  //   A
  //   sing
  //   in 2S
  //   8 bit Adder / Subtractor
  //   result
  //   ctr
endmodule
