// Logisim project 8bit_adder_subtractor.circ as structural Verilog: 1 circuit, main circuit main
module main (
  input  ctr,
  input  [7:0] in_2,
  input  [7:0] in_3,
  output c_out,
  output [7:0] sum
);

  wire adder_2_cout, adder_3_cout, adder_4_cout, adder_5_cout, adder_6_cout, adder_7_cout, adder_8_cout,
       and_1_out, not_1_out, xor_1_out, xor_2_out, xor_3_out, xor_4_out, xor_5_out, xor_6_out, xor_7_out,
       xor_8_out;

  xor xor_1 (xor_1_out, in_3[7], ctr);
  xor xor_2 (xor_2_out, in_3[6], ctr);
  Adder #(.width(1)) adder_1 (.a(xor_1_out), .b(in_2[7]), .out(sum[7]), .cin(adder_2_cout), .cout(c_out));
  not not_1 (not_1_out, c_out);
  and and_1 (and_1_out, not_1_out, ctr);
  LED led_1 (.in(and_1_out));
  xor xor_3 (xor_3_out, in_3[5], ctr);
  Adder #(.width(1)) adder_2 (.a(xor_2_out), .b(in_2[6]), .out(sum[6]), .cin(adder_3_cout), .cout(adder_2_cout));
  xor xor_4 (xor_4_out, in_3[4], ctr);
  Adder #(.width(1)) adder_3 (.a(xor_3_out), .b(in_2[5]), .out(sum[5]), .cin(adder_4_cout), .cout(adder_3_cout));
  xor xor_5 (xor_5_out, in_3[3], ctr);
  Adder #(.width(1)) adder_4 (.a(xor_4_out), .b(in_2[4]), .out(sum[4]), .cin(adder_5_cout), .cout(adder_4_cout));
  xor xor_6 (xor_6_out, in_3[2], ctr);
  Adder #(.width(1)) adder_5 (.a(xor_5_out), .b(in_2[3]), .out(sum[3]), .cin(adder_6_cout), .cout(adder_5_cout));
  xor xor_7 (xor_7_out, in_3[1], ctr);
  Adder #(.width(1)) adder_6 (.a(xor_6_out), .b(in_2[2]), .out(sum[2]), .cin(adder_7_cout), .cout(adder_6_cout));
  xor xor_8 (xor_8_out, in_3[0], ctr);
  Adder #(.width(1)) adder_7 (.a(xor_7_out), .b(in_2[1]), .out(sum[1]), .cin(adder_8_cout), .cout(adder_7_cout));
  Adder #(.width(1)) adder_8 (.a(xor_8_out), .b(in_2[0]), .out(sum[0]), .cin(ctr), .cout(adder_8_cout));

  // Notes on the sheet:
  //   A
  //   B
  //   in 2S
  //   8 bit Adder / Subtractor
endmodule
