// Logisim project 8x1_Mul.circ as structural Verilog: 1 circuit, main circuit main
module main (
  input  C,
  input  in_2,
  input  A,
  output out_4
);

  wire and_1_out, and_2_out, and_3_out, and_4_out, and_5_out, and_6_out, and_7_out, and_8_out, button_1_out,
       button_2_out, button_3_out, button_4_out, button_5_out, button_6_out, button_7_out, button_8_out,
       not_1_out, not_2_out, not_3_out, or_1_out, or_2_out;

  Button button_1 (.out(button_1_out));
  Button button_2 (.out(button_2_out));
  Button button_3 (.out(button_3_out));
  Button button_4 (.out(button_4_out));
  Button button_5 (.out(button_5_out));
  Button button_6 (.out(button_6_out));
  Button button_7 (.out(button_7_out));
  Button button_8 (.out(button_8_out));
  not not_1 (not_1_out, C);
  not not_2 (not_2_out, in_2);
  not not_3 (not_3_out, A);
  and and_1 (and_1_out, button_1_out, not_3_out, not_2_out, not_1_out);
  and and_2 (and_2_out, button_2_out, A, not_2_out, not_1_out);
  and and_3 (and_3_out, button_3_out, not_3_out, in_2, not_1_out);
  and and_4 (and_4_out, button_4_out, A, in_2, not_1_out);
  and and_5 (and_5_out, button_5_out, not_3_out, not_2_out, C);
  and and_6 (and_6_out, button_6_out, A, not_2_out, C);
  and and_7 (and_7_out, button_7_out, not_3_out, in_2, C);
  and and_8 (and_8_out, button_8_out, A, in_2, C);
  or or_1 (or_1_out, and_1_out, and_2_out, and_3_out, and_4_out);
  or or_2 (or_2_out, and_5_out, and_6_out, and_7_out, and_8_out);
  or or_3 (out_4, or_1_out, or_2_out);

  // Notes on the sheet:
  //   8 x 1 Multiplexer
  //   D0
  //   D1
  //   D2
  //   D3
  //   D4
  //   D5
  //   D6
  //   D7
  //   B
endmodule
