// Logisim project Adder_subtractor_using_IC.circ as structural Verilog: 1 circuit, main circuit main
module main (
  input  En_star,
  input  sub____1
);

  wire n74245_1_pin1, n74245_1_pin2, n74245_1_pin3, n74245_1_pin4, n74245_1_pin5, n74245_1_pin6,
       n74245_1_pin7, n74245_1_pin8, n74245_1_pin9, n74245_1_pin10, n74283_1_pin2, n74283_1_pin6,
       n74283_1_pin7, n74283_1_pin11, n74283_1_pin15, n74283_2_pin2, n74283_2_pin6, n74283_2_pin11,
       n74283_2_pin15;
  wire [7:0] n7486_1_pin12, n74245_1_pin18, n74283_2_pin5;

  _74245 #(.ShowInternalStructure("true"), .VccGndPorts("true")) u_74245_1 (
    .pin1(n74245_1_pin1), .pin2(n74245_1_pin2), .pin3(n74245_1_pin3), .pin4(n74245_1_pin4),
    .pin5(n74245_1_pin5), .pin6(n74245_1_pin6), .pin7(n74245_1_pin7), .pin8(n74245_1_pin8),
    .pin9(n74245_1_pin9), .pin10(n74245_1_pin10), .pin20(n74245_1_pin1), .pin19(En_star),
    .pin18(n74245_1_pin18[0]), .pin17(n74245_1_pin18[1]), .pin16(n74245_1_pin18[2]),
    .pin15(n74245_1_pin18[3]), .pin14(n74245_1_pin18[4]), .pin13(n74245_1_pin18[5]),
    .pin12(n74245_1_pin18[6]), .pin11(n74245_1_pin18[7]));
  LED led_1 (.in(n74245_1_pin2));
  LED led_2 (.in(n74245_1_pin3));
  LED led_3 (.in(n74245_1_pin4));
  LED led_4 (.in(n74245_1_pin5));
  LED led_5 (.in(n74245_1_pin6));
  LED led_6 (.in(n74245_1_pin7));
  LED led_7 (.in(n74245_1_pin8));
  LED led_8 (.in(n74245_1_pin9));
  _74283 #(.ShowInternalStructure("true"), .VccGndPorts("true")) u_74283_1 (
    .pin1(n74245_1_pin7), .pin2(n74283_1_pin2), .pin3(n74283_2_pin5[5]), .pin4(n74245_1_pin6),
    .pin5(n74283_2_pin5[4]), .pin6(n74283_1_pin6), .pin7(n74283_1_pin7), .pin8(n74245_1_pin10),
    .pin16(n74245_1_pin1), .pin15(n74283_1_pin15), .pin14(n74283_2_pin5[6]), .pin13(n74245_1_pin8),
    .pin12(n74283_2_pin5[7]), .pin11(n74283_1_pin11), .pin10(n74245_1_pin9));  // open: pin9
  _74283 #(.ShowInternalStructure("true"), .VccGndPorts("true")) u_74283_2 (
    .pin1(n74245_1_pin3), .pin2(n74283_2_pin2), .pin3(n74283_2_pin5[1]), .pin4(n74245_1_pin2),
    .pin5(n74283_2_pin5[0]), .pin6(n74283_2_pin6), .pin7(sub____1), .pin8(n74245_1_pin10),
    .pin16(n74245_1_pin1), .pin15(n74283_2_pin15), .pin14(n74283_2_pin5[2]), .pin13(n74245_1_pin4),
    .pin12(n74283_2_pin5[3]), .pin11(n74283_2_pin11), .pin10(n74245_1_pin5), .pin9(n74283_1_pin7));
  _7486 #(.ShowInternalStructure("true"), .VccGndPorts("true")) u_7486_1 (
    .pin1(sub____1), .pin2(n7486_1_pin12[7]), .pin3(n74283_1_pin11), .pin4(sub____1),
    .pin5(n7486_1_pin12[6]), .pin6(n74283_1_pin15), .pin7(n74245_1_pin10), .pin14(n74245_1_pin1),
    .pin13(sub____1), .pin12(n7486_1_pin12[0]), .pin11(n74283_2_pin6), .pin10(sub____1),
    .pin9(n7486_1_pin12[1]), .pin8(n74283_2_pin2));
  _7486 #(.ShowInternalStructure("true"), .VccGndPorts("true")) u_7486_2 (
    .pin1(sub____1), .pin2(n7486_1_pin12[5]), .pin3(n74283_1_pin2), .pin4(sub____1), .pin5(n7486_1_pin12[4]),
    .pin6(n74283_1_pin6), .pin7(n74245_1_pin10), .pin14(n74245_1_pin1), .pin13(sub____1),
    .pin12(n7486_1_pin12[2]), .pin11(n74283_2_pin15), .pin10(sub____1), .pin9(n7486_1_pin12[3]),
    .pin8(n74283_2_pin11));
  // also tied to GND on the sheet: n74245_1_pin10
  // also tied to VCC on the sheet: n74245_1_pin1

  // Notes on the sheet:
  //   En_star: pull=up
  //   dir
  //   0 ...7
  //   A registor
  //   c in is sub=1
  //   0
  //   7
  //   6
  //   1
  //   2
  //   5
  //   4
  //   3
  //   mode
endmodule
