// Logisim project Clock_with_hold_option.circ as structural Verilog: 1 circuit, main circuit main
module main (
);

  wire switch_1_p1, switch_1_p2, switch_2_p2, transistor_1_out;

  // Switch switch_1: pin names not known; wires that end beside it: switch_1_p1, switch_1_p2
  Clock clock_1 (.out(switch_1_p1));
  // Switch switch_2: pin names not known; wires that end beside it: 1'b1, switch_2_p2
  Pull_Resistor pull_resistor_1 (.node(switch_1_p2));
  Transistor transistor_1 (.in(switch_1_p1), .out(transistor_1_out), .gate(switch_1_p2));
  Pull_Resistor pull_resistor_2 (.node(switch_2_p2));
  Transistor transistor_2 (.in(1'b1), .out(transistor_1_out), .gate(switch_2_p2));
  LED led_1 (.in(transistor_1_out));
  Pull_Resistor pull_resistor_3 (.node(transistor_1_out));

  // Notes on the sheet:
  //   On/Off
  //   Hold
  //   Clock
endmodule
