// Logisim project AND.circ as structural Verilog: 1 circuit, main circuit main
module main (
  input  A,
  input  B,
  input  in_3,
  input  in_4,
  output out,
  output out_6
);

  wire nand_1_out, transistor_1_out, transistor_3_out;

  LED led_1 ();  // open: in
  LED led_2 ();  // open: in
  Transistor transistor_1 (.in(1'b1), .out(transistor_1_out), .gate(A));
  Transistor #(.\type ("n")) transistor_2 (.in(transistor_3_out), .out(transistor_1_out), .gate(A));
  Transistor #(.\type ("n")) transistor_3 (.in(1'b0), .out(transistor_3_out), .gate(B));
  Transistor transistor_4 (.in(1'b1), .out(transistor_1_out), .gate(B));
  LED led_3 (.in(transistor_1_out));
  Transistor transistor_5 (.in(1'b1), .out(out), .gate(transistor_1_out));
  LED led_4 (.in(out));
  Transistor #(.\type ("n")) transistor_6 (.in(1'b0), .out(out), .gate(transistor_1_out));
  LED led_5 (.in(in_3));
  LED led_6 (.in(in_4));
  nand nand_1 (nand_1_out, in_3, in_4);
  not not_1 (out_6, nand_1_out);
  LED led_7 (.in(out_6));

  // Notes on the sheet:
  //   AND
  //   Vcc
  //   GND
  //   O
  //   A B
  //   _________
  //   0 0 | 0
  //   0 1 | 0
  //   1 0 | 0
  //   1 1 | 1
endmodule
