// Logisim project CMOSBuffer.circ as structural Verilog: 1 circuit, main circuit main
module main (
  input  signal,
  output Stronger_Signal
);

  wire transistor_1_out;

  LED led_1 (.in(signal));
  Transistor transistor_1 (.in(1'b1), .out(transistor_1_out), .gate(signal));
  Transistor #(.\type ("n")) transistor_2 (.in(1'b0), .out(transistor_1_out), .gate(signal));
  Transistor transistor_3 (.in(1'b1), .out(Stronger_Signal), .gate(transistor_1_out));
  Transistor #(.\type ("n")) transistor_4 (.in(1'b0), .out(Stronger_Signal), .gate(transistor_1_out));
  LED led_2 (.in(Stronger_Signal));

  // Notes on the sheet:
  //   CMos BUFFER
  //   vcc
  //   GND
endmodule
