// Logisim project NAND.circ as structural Verilog: 1 circuit, main circuit main
module main (
  input  A,
  input  B,
  input  in_3,
  input  in_4,
  output out,
  output out_6
);

  wire transistor_3_out;

  LED led_1 (.in(A));
  LED led_2 (.in(B));
  Transistor transistor_1 (.in(1'b1), .out(out), .gate(A));
  Transistor #(.\type ("n")) transistor_2 (.in(transistor_3_out), .out(out), .gate(A));
  Transistor #(.\type ("n")) transistor_3 (.in(1'b0), .out(transistor_3_out), .gate(B));
  Transistor transistor_4 (.in(1'b1), .out(out), .gate(B));
  LED led_3 (.in(out));
  LED led_4 (.in(in_3));
  LED led_5 (.in(in_4));
  nand nand_1 (out_6, in_3, in_4);
  LED led_6 (.in(out_6));

  // Notes on the sheet:
  //   NAND
  //   VCC
  //   GND
  //   O
  //   A B
  //   _________
  //   0 0 | 1
  //   0 1 | 1
  //   1 0 | 1
  //   1 1 | 0
endmodule
