// Logisim project Not.circ as structural Verilog: 1 circuit, main circuit main
module main (
  input  In,
  input  in_2,
  output out,
  output out_4
);

  LED led_1 (.in(In));
  Transistor transistor_1 (.in(1'b1), .out(out), .gate(In));
  LED led_2 (.in(out));
  Transistor #(.\type ("n")) transistor_2 (.in(1'b0), .out(out), .gate(In));
  not not_1 (out_4, in_2);

  // Notes on the sheet:
  //   Not gate
  //   Vcc
  //   GND
  //   0 | 1
  //   1 | 0
endmodule
