// Logisim project TriState.circ as structural Verilog: 1 circuit, main circuit main
module main (
  input  enable,
  input  in,
  output out_3
);

  wire not_1_out, not_2_out, not_3_out, transistor_1_out;

  not not_1 (not_1_out, in);
  Transistor transistor_1 (.in(in), .out(transistor_1_out), .gate(not_1_out));
  not not_2 (not_2_out, in);
  not not_3 (not_3_out, enable);
  Transistor transistor_2 (.in(transistor_1_out), .out(out_3), .gate(not_3_out));
  Transistor #(.\type ("n")) transistor_3 (.in(1'b0), .out(transistor_1_out), .gate(not_2_out));

  // Notes on the sheet:
  //   Tristate gates
endmodule
