// Logisim project XNOR.circ as structural Verilog: 1 circuit, main circuit main
module main (
  input  A,
  input  [1:0] in_2,
  input  B,
  output out_4,
  output out_5
);

  wire transistor_1_out, transistor_4_out, transistor_5_out, transistor_6_out, transistor_9_out,
       transistor_11_out, transistor_12_out, transistor_16_out, transistor_19_out, transistor_20_out,
       transistor_23_out;

  LED led_1 (.in(A));
  LED led_2 (.in(B));
  Transistor transistor_1 (.in(1'b1), .out(transistor_1_out), .gate(transistor_5_out));
  Transistor transistor_2 (.in(1'b1), .out(transistor_1_out), .gate(B));
  Transistor #(.\type ("n")) transistor_3 (.in(transistor_4_out), .out(transistor_1_out), .gate(transistor_5_out));
  Transistor #(.\type ("n")) transistor_4 (.in(1'b0), .out(transistor_4_out), .gate(B));
  Transistor transistor_5 (.in(1'b1), .out(transistor_5_out), .gate(A));
  Transistor transistor_6 (.in(1'b1), .out(transistor_6_out), .gate(B));
  Transistor #(.\type ("n")) transistor_7 (.in(1'b0), .out(transistor_5_out), .gate(A));
  Transistor #(.\type ("n")) transistor_8 (.in(1'b0), .out(transistor_6_out), .gate(B));
  Transistor transistor_9 (.in(1'b1), .out(transistor_9_out), .gate(transistor_1_out));
  Transistor #(.\type ("n")) transistor_10 (.in(1'b0), .out(transistor_9_out), .gate(transistor_1_out));
  Transistor transistor_11 (.in(1'b1), .out(transistor_11_out), .gate(A));
  Transistor transistor_12 (.in(1'b1), .out(transistor_12_out), .gate(transistor_11_out));
  Transistor transistor_13 (.in(1'b1), .out(transistor_11_out), .gate(transistor_6_out));
  Transistor #(.\type ("n")) transistor_14 (.in(transistor_16_out), .out(transistor_11_out), .gate(A));
  Transistor #(.\type ("n")) transistor_15 (.in(1'b0), .out(transistor_12_out), .gate(transistor_11_out));
  Transistor #(.\type ("n")) transistor_16 (.in(1'b0), .out(transistor_16_out), .gate(transistor_6_out));
  LED led_3 (.in(transistor_5_out));
  LED led_4 (.in(transistor_6_out));
  Transistor transistor_17 (.in(1'b1), .out(out_5), .gate(transistor_23_out));
  Transistor #(.\type ("n")) transistor_18 (.in(1'b0), .out(out_5), .gate(transistor_23_out));
  LED led_5 (.in(out_5));
  Transistor transistor_19 (.in(1'b1), .out(transistor_19_out), .gate(transistor_9_out));
  Transistor transistor_20 (.in(transistor_19_out), .out(transistor_20_out), .gate(transistor_12_out));
  Transistor #(.\type ("n")) transistor_21 (.in(1'b0), .out(transistor_20_out), .gate(transistor_9_out));
  Transistor #(.\type ("n")) transistor_22 (.in(1'b0), .out(transistor_20_out), .gate(transistor_12_out));
  Transistor transistor_23 (.in(1'b1), .out(transistor_23_out), .gate(transistor_20_out));
  Transistor #(.\type ("n")) transistor_24 (.in(1'b0), .out(transistor_23_out), .gate(transistor_20_out));
  LED led_6 (.in(in_2[0]));
  LED led_7 (.in(in_2[1]));
  xnor xnor_1 (out_4, in_2[0], in_2[1]);
  LED led_8 (.in(out_4));

  // Notes on the sheet:
  //   XNOR
  //   GND
  //   NOT
  //   AND
  //   Vcc
  //   AND
  //   A*
  //   B*
  //   OR
  //   (A*B + AB*)*
  //   A B
  //   O
  //   _________
  //   0 0 | 1
  //   0 1 | 0
  //   1 0 | 0
  //   1 1 | 1
endmodule
