// Logisim project static_Ram_8bit.circ as structural Verilog: 1 circuit, main circuit main
module main (
);

  wire n74245_1_pin1, n74245_1_pin19, n74245_2_pin1, n74245_2_pin2, n74245_2_pin3, n74245_2_pin4,
       n74245_2_pin5, n74245_2_pin6, n74245_2_pin10, n74245_2_pin19, n74245_3_pin1, n74245_3_pin10,
       n74245_3_pin19, register_1_q, register_3_q, register_4_q, undriven, undriven_2, undriven_3,
       undriven_4, undriven_5, undriven_6;
  wire [7:0] n74245_1_pin18, n74245_2_pin18, register_2_q, register_9_q;

  Register #(.width(1)) register_1 (
    .D(n74245_2_pin18[7]), .en(undriven_3), .clk(undriven_4), .Q(register_1_q));  // open: clr
  Register register_2 (.D(n74245_1_pin18), .en(undriven_2), .clk(undriven), .Q(register_2_q));  // open: clr
  Register #(.width(1)) register_3 (
    .D(n74245_2_pin18[6]), .en(undriven_3), .clk(undriven_4), .Q(register_3_q));  // open: clr
  _74245 #(.ShowInternalStructure("true"), .VccGndPorts("true")) u_74245_1 (
    .pin1(n74245_1_pin1), .pin2(register_2_q[0]), .pin3(register_2_q[1]), .pin4(register_2_q[2]),
    .pin5(register_2_q[3]), .pin6(register_2_q[4]), .pin7(register_2_q[5]), .pin8(register_2_q[6]),
    .pin9(register_2_q[7]), .pin20(n74245_1_pin1), .pin19(n74245_1_pin19), .pin18(n74245_1_pin18[0]),
    .pin17(n74245_1_pin18[1]), .pin16(n74245_1_pin18[2]), .pin15(n74245_1_pin18[3]),
    .pin14(n74245_1_pin18[4]), .pin13(n74245_1_pin18[5]), .pin12(n74245_1_pin18[6]), .pin11(n74245_1_pin18[7]));  // open: pin10
  Register #(.width(1)) register_4 (
    .D(n74245_2_pin18[5]), .en(undriven_3), .clk(undriven_4), .Q(register_4_q));  // open: clr
  _74245 #(.ShowInternalStructure("true"), .VccGndPorts("true")) u_74245_2 (
    .pin1(n74245_2_pin1), .pin2(n74245_2_pin2), .pin3(n74245_2_pin3), .pin4(n74245_2_pin4),
    .pin5(n74245_2_pin5), .pin6(n74245_2_pin6), .pin7(register_4_q), .pin8(register_3_q),
    .pin9(register_1_q), .pin10(n74245_2_pin10), .pin20(n74245_2_pin1), .pin19(n74245_2_pin19),
    .pin18(n74245_2_pin18[0]), .pin17(n74245_2_pin18[1]), .pin16(n74245_2_pin18[2]),
    .pin15(n74245_2_pin18[3]), .pin14(n74245_2_pin18[4]), .pin13(n74245_2_pin18[5]),
    .pin12(n74245_2_pin18[6]), .pin11(n74245_2_pin18[7]));
  Register #(.width(1)) register_5 (
    .D(n74245_2_pin18[4]), .en(undriven_3), .clk(undriven_4), .Q(n74245_2_pin6));  // open: clr
  Register #(.width(1)) register_6 (
    .D(n74245_2_pin18[3]), .en(undriven_3), .clk(undriven_4), .Q(n74245_2_pin5));  // open: clr
  Register #(.width(1)) register_7 (
    .D(n74245_2_pin18[2]), .en(undriven_3), .clk(undriven_4), .Q(n74245_2_pin4));  // open: clr
  Register #(.width(1)) register_8 (
    .D(n74245_2_pin18[1]), .en(undriven_3), .clk(undriven_4), .Q(n74245_2_pin3));  // open: clr
  Register register_9 (.D(register_9_q), .en(undriven_5), .clk(undriven_6), .Q(register_9_q));  // open: clr
  Register #(.width(1)) register_10 (
    .D(n74245_2_pin18[0]), .en(undriven_3), .clk(undriven_4), .Q(n74245_2_pin2));  // open: clr
  _74245 #(.ShowInternalStructure("true"), .VccGndPorts("true")) u_74245_3 (
    .pin1(n74245_3_pin1), .pin2(register_9_q[0]), .pin3(register_9_q[1]), .pin4(register_9_q[2]),
    .pin5(register_9_q[3]), .pin6(register_9_q[4]), .pin7(register_9_q[5]), .pin8(register_9_q[6]),
    .pin9(register_9_q[7]), .pin10(n74245_3_pin10), .pin20(n74245_3_pin1), .pin19(n74245_3_pin19),
    .pin18(register_9_q[0]), .pin17(register_9_q[1]), .pin16(register_9_q[2]), .pin15(register_9_q[3]),
    .pin14(register_9_q[4]), .pin13(register_9_q[5]), .pin12(register_9_q[6]), .pin11(register_9_q[7]));
  RAM ram_1 ();  // open: addr, we, oe, clk, din, dout
  // also tied to GND on the sheet: n74245_2_pin10
  // also tied to VCC on the sheet: n74245_2_pin1

  // Notes on the sheet:
  //   bus
  //   en*
  //   load
  //   clk
  //   vcc
  //   enable*
  //   clk
  //   load
  //   GND
  //   bus
  //   en*
  //   clk
  //   load
endmodule
