// Logisim project 8_bit_shift_Register.circ as structural Verilog: 1 circuit, main circuit main
module main (
  input  in_1,
  output [7:0] out_2
);

  wire clock_1_out;

  Clock clock_1 (.out(clock_1_out));
  D_Flip_Flop d_ff_1 (.D(in_1), .clk(clock_1_out), .Q(out_2[7]));  // open: Qn, preset, reset
  D_Flip_Flop d_ff_2 (.D(out_2[7]), .clk(clock_1_out), .Q(out_2[6]));  // open: Qn, preset, reset
  D_Flip_Flop d_ff_3 (.D(out_2[6]), .clk(clock_1_out), .Q(out_2[5]));  // open: Qn, preset, reset
  D_Flip_Flop d_ff_4 (.D(out_2[5]), .clk(clock_1_out), .Q(out_2[4]));  // open: Qn, preset, reset
  D_Flip_Flop d_ff_5 (.D(out_2[4]), .clk(clock_1_out), .Q(out_2[3]));  // open: Qn, preset, reset
  D_Flip_Flop d_ff_6 (.D(out_2[3]), .clk(clock_1_out), .Q(out_2[2]));  // open: Qn, preset, reset
  D_Flip_Flop d_ff_7 (.D(out_2[2]), .clk(clock_1_out), .Q(out_2[1]));  // open: Qn, preset, reset
  D_Flip_Flop d_ff_8 (.D(out_2[1]), .clk(clock_1_out), .Q(out_2[0]));  // open: Qn, preset, reset

  // Notes on the sheet:
  //   8 bit Shift Register
endmodule
