// Logisim project 8_bit_usign_D.circ as structural Verilog: 1 circuit, main circuit main
module main (
  input  load,
  input  [7:0] in_2,
  output [7:0] \output 
);

  wire and_1_out, and_2_out, and_3_out, and_4_out, and_5_out, and_6_out, and_7_out, and_8_out, and_9_out,
       and_10_out, and_11_out, and_12_out, and_13_out, and_14_out, and_15_out, and_16_out, clock_1_out,
       not_1_out, not_2_out, not_3_out, not_4_out, not_5_out, not_6_out, not_7_out, not_8_out, or_1_out,
       or_2_out, or_3_out, or_4_out, or_5_out, or_6_out, or_7_out, or_8_out;

  Clock clock_1 (.out(clock_1_out));
  not not_1 (not_1_out, load);
  not not_2 (not_2_out, load);
  not not_3 (not_3_out, load);
  not not_4 (not_4_out, load);
  not not_5 (not_5_out, load);
  not not_6 (not_6_out, load);
  not not_7 (not_7_out, load);
  not not_8 (not_8_out, load);
  and and_1 (and_1_out, \output [0], not_1_out);
  and and_2 (and_2_out, load, in_2[0]);
  and and_3 (and_3_out, \output [1], not_2_out);
  and and_4 (and_4_out, load, in_2[1]);
  and and_5 (and_5_out, \output [2], not_3_out);
  and and_6 (and_6_out, load, in_2[2]);
  and and_7 (and_7_out, \output [3], not_4_out);
  and and_8 (and_8_out, load, in_2[3]);
  and and_9 (and_9_out, \output [4], not_5_out);
  and and_10 (and_10_out, load, in_2[4]);
  and and_11 (and_11_out, \output [5], not_6_out);
  and and_12 (and_12_out, load, in_2[5]);
  and and_13 (and_13_out, \output [6], not_7_out);
  and and_14 (and_14_out, load, in_2[6]);
  and and_15 (and_15_out, \output [7], not_8_out);
  and and_16 (and_16_out, load, in_2[7]);
  or or_1 (or_1_out, and_1_out, and_2_out);
  or or_2 (or_2_out, and_3_out, and_4_out);
  or or_3 (or_3_out, and_5_out, and_6_out);
  or or_4 (or_4_out, and_7_out, and_8_out);
  or or_5 (or_5_out, and_9_out, and_10_out);
  or or_6 (or_6_out, and_11_out, and_12_out);
  or or_7 (or_7_out, and_13_out, and_14_out);
  or or_8 (or_8_out, and_15_out, and_16_out);
  D_Flip_Flop d_ff_1 (.D(or_1_out), .clk(clock_1_out), .Q(\output [0]));  // open: Qn, preset, reset
  D_Flip_Flop d_ff_2 (.D(or_2_out), .clk(clock_1_out), .Q(\output [1]));  // open: Qn, preset, reset
  D_Flip_Flop d_ff_3 (.D(or_3_out), .clk(clock_1_out), .Q(\output [2]));  // open: Qn, preset, reset
  D_Flip_Flop d_ff_4 (.D(or_4_out), .clk(clock_1_out), .Q(\output [3]));  // open: Qn, preset, reset
  D_Flip_Flop d_ff_5 (.D(or_5_out), .clk(clock_1_out), .Q(\output [4]));  // open: Qn, preset, reset
  D_Flip_Flop d_ff_6 (.D(or_6_out), .clk(clock_1_out), .Q(\output [5]));  // open: Qn, preset, reset
  D_Flip_Flop d_ff_7 (.D(or_7_out), .clk(clock_1_out), .Q(\output [6]));  // open: Qn, preset, reset
  D_Flip_Flop d_ff_8 (.D(or_8_out), .clk(clock_1_out), .Q(\output [7]));  // open: Qn, preset, reset

  // Notes on the sheet:
  //   8 bit Register
  //   clk
  //   input
endmodule
