// Logisim project 8bit_shift_register_IC74175.circ as structural Verilog: 1 circuit, main circuit main
module main (
  input  in_1
);

  wire clock_1_out, n74175_1_pin2;
  wire [6:0] n74175_2_pin15;

  Clock clock_1 (.out(clock_1_out));
  _74175 u_74175_1 (
    .pin2(n74175_1_pin2), .pin4(in_1), .pin5(n74175_1_pin2), .pin7(n74175_2_pin15[6]),
    .pin15(n74175_2_pin15[4]), .pin13(n74175_2_pin15[5]), .pin12(n74175_2_pin15[6]),
    .pin10(n74175_2_pin15[5]), .pin9(clock_1_out));  // open: pin1, pin3, pin6, pin14, pin11
  _74175 u_74175_2 (
    .pin2(n74175_2_pin15[3]), .pin4(n74175_2_pin15[4]), .pin5(n74175_2_pin15[3]), .pin7(n74175_2_pin15[2]),
    .pin15(n74175_2_pin15[0]), .pin13(n74175_2_pin15[1]), .pin12(n74175_2_pin15[2]),
    .pin10(n74175_2_pin15[1]), .pin9(clock_1_out));  // open: pin1, pin3, pin6, pin14, pin11

  // Notes on the sheet:
  //   Shift Register
endmodule
