// Logisim project Complete_8bit_Register_bus.circ as structural Verilog: 1 circuit, main circuit main
module main (
  input  load,
  input  enable_star
);

  wire button_1_out, clock_1_out, n74245_1_pin1, n74245_1_pin10;
  wire [7:0] n74245_1_pin18, register_1_q;

  Clock clock_1 (.out(clock_1_out));
  LED led_1 (.in(clock_1_out));
  Button button_1 (.out(button_1_out));
  Register register_1 (.D(n74245_1_pin18), .en(load), .clk(clock_1_out), .Q(register_1_q), .clr(button_1_out));
  LED led_2 (.in(register_1_q[0]));
  LED led_3 (.in(register_1_q[1]));
  LED led_4 (.in(register_1_q[2]));
  LED led_5 (.in(register_1_q[3]));
  LED led_6 (.in(register_1_q[4]));
  LED led_7 (.in(register_1_q[5]));
  LED led_8 (.in(register_1_q[6]));
  LED led_9 (.in(register_1_q[7]));
  _74245 #(.VccGndPorts("true")) u_74245_1 (
    .pin1(n74245_1_pin1), .pin2(register_1_q[0]), .pin3(register_1_q[1]), .pin4(register_1_q[2]),
    .pin5(register_1_q[3]), .pin6(register_1_q[4]), .pin7(register_1_q[5]), .pin8(register_1_q[6]),
    .pin9(register_1_q[7]), .pin10(n74245_1_pin10), .pin20(n74245_1_pin1), .pin19(enable_star),
    .pin18(n74245_1_pin18[0]), .pin17(n74245_1_pin18[1]), .pin16(n74245_1_pin18[2]),
    .pin15(n74245_1_pin18[3]), .pin14(n74245_1_pin18[4]), .pin13(n74245_1_pin18[5]),
    .pin12(n74245_1_pin18[6]), .pin11(n74245_1_pin18[7]));
  // also tied to GND on the sheet: n74245_1_pin10
  // also tied to VCC on the sheet: n74245_1_pin1

  // Notes on the sheet:
  //   Complete Register 8bit
  //   8 bit bus
  //   clr
endmodule
