// Logisim project 3bit_UP_using_JK.circ as structural Verilog: 1 circuit, main circuit main
module main (
  output out_1,
  output out_2,
  output out_3,
  output [2:0] out_4,
  output out_5,
  output out_6,
  output out_7
);

  wire and_1_out, button_1_out, clock_1_out, clock_2_out, clock_3_out, j_k_ff_3_qn, j_k_ff_5_qn, j_k_ff_7_qn,
       j_k_ff_8_qn, switch_1_p2, switch_2_p4;

  // Switch switch_1: pin names not known; wires that end beside it: 1'b1, switch_1_p2
  Clock clock_1 (.out(clock_1_out));
  J_K_Flip_Flop j_k_ff_1 (.J(switch_1_p2), .K(switch_1_p2), .clk(clock_1_out), .Q(out_3));  // open: Qn, preset, reset
  Button button_1 (.out(button_1_out));
  Clock clock_2 (.out(clock_2_out));
  J_K_Flip_Flop j_k_ff_2 (.J(out_3), .K(out_3), .clk(clock_1_out), .Q(out_2));  // open: Qn, preset, reset
  LED led_1 (.in(out_5));
  J_K_Flip_Flop j_k_ff_3 (
    .J(button_1_out), .K(button_1_out), .clk(clock_2_out), .Q(out_7), .Qn(j_k_ff_3_qn));  // open: preset, reset
  and and_1 (and_1_out, out_3, out_2);
  J_K_Flip_Flop j_k_ff_4 (.J(and_1_out), .K(and_1_out), .clk(clock_1_out), .Q(out_1));  // open: Qn, preset, reset
  LED led_2 (.in(out_6));
  J_K_Flip_Flop j_k_ff_5 (
    .J(button_1_out), .K(button_1_out), .clk(j_k_ff_3_qn), .Q(out_6), .Qn(j_k_ff_5_qn));  // open: preset, reset
  LED led_3 (.in(out_7));
  J_K_Flip_Flop j_k_ff_6 (.J(button_1_out), .K(button_1_out), .clk(j_k_ff_5_qn), .Q(out_5));  // open: Qn, preset, reset
  // Switch switch_2: pin names not known; wires that end beside it: j_k_ff_3_qn, j_k_ff_5_qn, 1'b1, switch_2_p4, switch_2_p4
  Clock clock_3 (.out(clock_3_out));
  J_K_Flip_Flop j_k_ff_7 (
    .J(switch_2_p4), .K(switch_2_p4), .clk(clock_3_out), .Q(out_4[0]), .Qn(j_k_ff_7_qn));  // open: preset, reset
  J_K_Flip_Flop j_k_ff_8 (
    .J(switch_2_p4), .K(switch_2_p4), .clk(j_k_ff_7_qn), .Q(out_4[1]), .Qn(j_k_ff_8_qn));  // open: preset, reset
  J_K_Flip_Flop j_k_ff_9 (
    .J(switch_2_p4), .K(switch_2_p4), .clk(j_k_ff_8_qn), .Q(out_4[2]));  // open: Qn, preset, reset
endmodule
