// Logisim project 3bit_down_counter.circ as structural Verilog: 1 circuit, main circuit main
module main (
  input  in_1,
  output out_2,
  output out_3,
  output out_4
);

  wire and_1_out, and_2_out, and_3_out, and_4_out, and_5_out, and_6_out, and_7_out, and_8_out, and_9_out,
       and_10_out, and_11_out, and_12_out, clock_1_out, nor_1_out, nor_2_out, nor_4_out, nor_5_out,
       nor_6_out, nor_8_out, nor_9_out, nor_10_out, nor_12_out, not_1_out, not_2_out, not_3_out, not_4_out;

  Clock clock_1 (.out(clock_1_out));
  not not_1 (not_1_out, clock_1_out);
  and and_1 (and_1_out, nor_4_out, in_1, not_1_out);
  and and_2 (and_2_out, not_1_out, in_1, out_4);
  nor nor_1 (nor_1_out, and_1_out, nor_2_out);
  LED led_1 (.in(nor_1_out));
  nor nor_2 (nor_2_out, nor_1_out, and_2_out);
  LED led_2 (.in(nor_2_out));
  LED led_3 (.in(out_2));
  not not_2 (not_2_out, not_1_out);
  LED led_4 (.in(out_3));
  LED led_5 (.in(out_4));
  and and_3 (and_3_out, nor_1_out, not_2_out);
  and and_4 (and_4_out, not_2_out, nor_2_out);
  nor nor_3 (out_4, and_3_out, nor_4_out);
  nor nor_4 (nor_4_out, out_4, and_4_out);
  LED led_6 (.in(out_4));
  LED led_7 (.in(nor_4_out));
  and and_5 (and_5_out, nor_8_out, in_1, nor_4_out);
  and and_6 (and_6_out, nor_4_out, in_1, out_3);
  nor nor_5 (nor_5_out, and_5_out, nor_6_out);
  LED led_8 (.in(nor_5_out));
  nor nor_6 (nor_6_out, nor_5_out, and_6_out);
  LED led_9 (.in(nor_6_out));
  not not_3 (not_3_out, nor_4_out);
  and and_7 (and_7_out, nor_5_out, not_3_out);
  and and_8 (and_8_out, not_3_out, nor_6_out);
  nor nor_7 (out_3, and_7_out, nor_8_out);
  nor nor_8 (nor_8_out, out_3, and_8_out);
  LED led_10 (.in(out_3));
  LED led_11 (.in(nor_8_out));
  and and_9 (and_9_out, nor_12_out, in_1, nor_8_out);
  and and_10 (and_10_out, nor_8_out, in_1, out_2);
  nor nor_9 (nor_9_out, and_9_out, nor_10_out);
  nor nor_10 (nor_10_out, nor_9_out, and_10_out);
  LED led_12 (.in(nor_9_out));
  LED led_13 (.in(nor_10_out));
  not not_4 (not_4_out, nor_8_out);
  and and_11 (and_11_out, nor_9_out, not_4_out);
  and and_12 (and_12_out, not_4_out, nor_10_out);
  nor nor_11 (out_2, and_11_out, nor_12_out);
  nor nor_12 (nor_12_out, out_2, and_12_out);
  LED led_14 (.in(out_2));

  // Notes on the sheet:
  //   clk
  //   S
  //   R
  //   clk 1 active
  //   Q*
  //   Q
  //   R
  //   S
  //   clk 0 active
  //   S
  //   R
  //   clk 1 active
  //   Q*
  //   Q
  //   R
  //   S
  //   clk 0 active
  //   S
  //   R
  //   clk 1 active
  //   Q
  //   Q*
  //   R
  //   S
  //   clk 0 active
endmodule
