// Logisim project 4bit_program_Counter.circ as structural Verilog: 1 circuit, main circuit main
module main (
  input  count_en,
  input  count_out_star,
  input  Load_star,
  input  [3:0] Load,
  output [7:0] out_5
);

  wire clock_1_out, n74161_1_pin8, n74161_1_pin16, n74245_1_pin1, n74245_1_pin11, n74245_1_pin12,
       n74245_1_pin13, n74245_1_pin14, n74245_1_pin18, n74245_1_pin20;

  Clock clock_1 (.out(clock_1_out));
  _74245 #(.ShowInternalStructure("true"), .VccGndPorts("true")) u_74245_1 (
    .pin1(n74245_1_pin1), .pin2(out_5[7]), .pin3(out_5[6]), .pin4(out_5[5]), .pin5(out_5[4]),
    .pin6(out_5[3]), .pin7(out_5[2]), .pin8(out_5[1]), .pin9(out_5[0]), .pin10(n74245_1_pin1),
    .pin20(n74245_1_pin20), .pin19(count_out_star), .pin18(n74245_1_pin18), .pin17(n74245_1_pin18),
    .pin16(n74245_1_pin18), .pin15(n74245_1_pin18), .pin14(n74245_1_pin14), .pin13(n74245_1_pin13),
    .pin12(n74245_1_pin12), .pin11(n74245_1_pin11));
  _74161 #(.ShowInternalStructure("true"), .VccGndPorts("true")) u_74161_1 (
    .pin2(clock_1_out), .pin3(Load[0]), .pin4(Load[1]), .pin5(Load[2]), .pin6(Load[3]), .pin7(count_en),
    .pin8(n74161_1_pin8), .pin16(n74161_1_pin16), .pin14(n74245_1_pin11), .pin13(n74245_1_pin12),
    .pin12(n74245_1_pin13), .pin11(n74245_1_pin14), .pin10(count_en), .pin9(Load_star));  // open: pin1, pin15
  // also tied to GND on the sheet: {n74245_1_pin18, n74245_1_pin1, n74161_1_pin8}
  // also tied to VCC on the sheet: {n74245_1_pin20, n74161_1_pin16}

  // Notes on the sheet:
  //   Program Counter
endmodule
