// Logisim project 8_bit.circ_v1.circ as structural Verilog: 1 circuit, main circuit main
module main (
  input  [7:0] in_1,
  output [7:0] out_2
);

  wire button_1_out, clock_1_out, j_k_ff_1_qn, j_k_ff_2_qn, j_k_ff_3_qn, j_k_ff_4_qn, j_k_ff_5_qn,
       j_k_ff_6_qn, j_k_ff_7_qn, switch_1_p2;

  Button button_1 (.out(button_1_out));
  // Switch switch_1: pin names not known; wires that end beside it: 1'b1, switch_1_p2, switch_1_p2
  J_K_Flip_Flop j_k_ff_1 (
    .J(switch_1_p2), .K(switch_1_p2), .clk(clock_1_out), .Q(out_2[0]), .Qn(j_k_ff_1_qn), .preset(in_1[0]),
    .reset(button_1_out));
  Clock clock_1 (.out(clock_1_out));
  J_K_Flip_Flop j_k_ff_2 (
    .J(switch_1_p2), .K(switch_1_p2), .clk(j_k_ff_1_qn), .Q(out_2[1]), .Qn(j_k_ff_2_qn), .preset(in_1[1]),
    .reset(button_1_out));
  J_K_Flip_Flop j_k_ff_3 (
    .J(switch_1_p2), .K(switch_1_p2), .clk(j_k_ff_2_qn), .Q(out_2[2]), .Qn(j_k_ff_3_qn), .preset(in_1[2]),
    .reset(button_1_out));
  J_K_Flip_Flop j_k_ff_4 (
    .J(switch_1_p2), .K(switch_1_p2), .clk(j_k_ff_3_qn), .Q(out_2[3]), .Qn(j_k_ff_4_qn), .preset(in_1[3]),
    .reset(button_1_out));
  J_K_Flip_Flop j_k_ff_5 (
    .J(switch_1_p2), .K(switch_1_p2), .clk(j_k_ff_4_qn), .Q(out_2[4]), .Qn(j_k_ff_5_qn), .preset(in_1[4]),
    .reset(button_1_out));
  J_K_Flip_Flop j_k_ff_6 (
    .J(switch_1_p2), .K(switch_1_p2), .clk(j_k_ff_5_qn), .Q(out_2[5]), .Qn(j_k_ff_6_qn), .preset(in_1[5]),
    .reset(button_1_out));
  J_K_Flip_Flop j_k_ff_7 (
    .J(switch_1_p2), .K(switch_1_p2), .clk(j_k_ff_6_qn), .Q(out_2[6]), .Qn(j_k_ff_7_qn), .preset(in_1[6]),
    .reset(button_1_out));
  J_K_Flip_Flop j_k_ff_8 (
    .J(switch_1_p2), .K(switch_1_p2), .clk(j_k_ff_7_qn), .Q(out_2[7]), .preset(in_1[7]), .reset(button_1_out));  // open: Qn

  // Notes on the sheet:
  //   set
  //   en
  //   clk
  //   R
  //   8 bit counter 
endmodule
