// Logisim project Working_3digit_7segment_disp_with_Rom.circ as structural Verilog: 1 circuit, main circuit main
module main (
);

  wire button_1_out, clock_1_out, j_k_ff_1_qn, j_k_ff_2_qn, j_k_ff_3_qn, j_k_ff_4_qn, j_k_ff_5_qn,
       j_k_ff_6_qn, j_k_ff_7_qn, switch_1_p2;
  wire [6:6] button_2_out;
  wire [7:0] j_k_ff_1_q, rom_1_data, rom_1_data_2, rom_1_data_3;
  wire [31:24] rom_1_data_4;

  // Switch switch_1: pin names not known; wires that end beside it: 1'b1, switch_1_p2, switch_1_p2
  Button button_1 (.out(button_1_out));
  Button #(.press("passive")) button_2 (.out(button_2_out[6]));
  J_K_Flip_Flop j_k_ff_1 (
    .J(switch_1_p2), .K(switch_1_p2), .clk(clock_1_out), .Q(j_k_ff_1_q[0]), .Qn(j_k_ff_1_qn),
    .reset(button_1_out));  // open: preset
  Clock clock_1 (.out(clock_1_out));
  J_K_Flip_Flop j_k_ff_2 (
    .J(switch_1_p2), .K(switch_1_p2), .clk(j_k_ff_1_qn), .Q(j_k_ff_1_q[1]), .Qn(j_k_ff_2_qn),
    .reset(button_1_out));  // open: preset
  J_K_Flip_Flop j_k_ff_3 (
    .J(switch_1_p2), .K(switch_1_p2), .clk(j_k_ff_2_qn), .Q(j_k_ff_1_q[2]), .Qn(j_k_ff_3_qn),
    .reset(button_1_out));  // open: preset
  J_K_Flip_Flop j_k_ff_4 (
    .J(switch_1_p2), .K(switch_1_p2), .clk(j_k_ff_3_qn), .Q(j_k_ff_1_q[3]), .Qn(j_k_ff_4_qn),
    .reset(button_1_out));  // open: preset
  _7_Segment_Display #(.active("false")) u_7_segment_display_1 (
    .g(button_2_out[6]), .f(1'b1), .a(1'b1), .b(1'b1), .e(1'b1), .d(1'b1), .c(1'b1), .dp(1'b1));
  _7_Segment_Display #(.active("false")) u_7_segment_display_2 (
    .g(rom_1_data_3[6]), .f(rom_1_data_3[5]), .a(rom_1_data_3[0]), .b(rom_1_data_3[1]), .e(rom_1_data_3[4]),
    .d(rom_1_data_3[3]), .c(rom_1_data_3[2]), .dp(rom_1_data_3[7]));
  J_K_Flip_Flop j_k_ff_5 (
    .J(switch_1_p2), .K(switch_1_p2), .clk(j_k_ff_4_qn), .Q(j_k_ff_1_q[4]), .Qn(j_k_ff_5_qn),
    .reset(button_1_out));  // open: preset
  _7_Segment_Display #(.active("false")) u_7_segment_display_3 (
    .g(rom_1_data_2[6]), .f(rom_1_data_2[5]), .a(rom_1_data_2[0]), .b(rom_1_data_2[1]), .e(rom_1_data_2[4]),
    .d(rom_1_data_2[3]), .c(rom_1_data_2[2]), .dp(rom_1_data_2[7]));
  _7_Segment_Display #(.active("false")) u_7_segment_display_4 (
    .g(rom_1_data[6]), .f(rom_1_data[5]), .a(rom_1_data[0]), .b(rom_1_data[1]), .e(rom_1_data[4]),
    .d(rom_1_data[3]), .c(rom_1_data[2]), .dp(rom_1_data[7]));
  J_K_Flip_Flop j_k_ff_6 (
    .J(switch_1_p2), .K(switch_1_p2), .clk(j_k_ff_5_qn), .Q(j_k_ff_1_q[5]), .Qn(j_k_ff_6_qn),
    .reset(button_1_out));  // open: preset
  ROM #(.dataWidth(32)) rom_1 (.addr(j_k_ff_1_q), .data({rom_1_data_4, rom_1_data_3, rom_1_data_2, rom_1_data}));
  J_K_Flip_Flop j_k_ff_7 (
    .J(switch_1_p2), .K(switch_1_p2), .clk(j_k_ff_6_qn), .Q(j_k_ff_1_q[6]), .Qn(j_k_ff_7_qn),
    .reset(button_1_out));  // open: preset
  J_K_Flip_Flop j_k_ff_8 (
    .J(switch_1_p2), .K(switch_1_p2), .clk(j_k_ff_7_qn), .Q(j_k_ff_1_q[7]), .reset(button_1_out));  // open: Qn, preset

  // Notes on the sheet:
  //   clk
  //   R
  //   Negetive
  //   contents of rom_1 (hex, n*v repeats v):
  //   c0c0c0 c0c0f9 c0c0a4 c0c0b0 c0c099 c0c092 c0c082 c0c0f8 c0c080 c0c090 c0f9c0 c0f9f9 c0f9a4 c0f9b0
  //   c0f999 c0f992 c0f982 c0f9f8 c0f980 c0f990 c0a4c0 c0a4f9 c0a4a4 c0a4b0 c0a499 c0a492 c0a482 c0a4f8
  //   c0a480 c0a490 c0b0c0 c0b0f9 c0b0a4 c0b0b0 c0b099 c0b092 c0b082 c0b0f8 c0b080 c0b090 c099c0 c099f9
  //   c099a4 c099b0 c09999 c09992 c09982 c099f8 c09980 c09990 c092c0 c092f9 c092a4 c092b0 c09299 c09292
  //   c09282 c092f8 c09280 c09290 c082c0 c082f9 c082a4 c082b0 c08299 c08292 c08282 c082f8 c08280 c08290
  //   c0f8c0 c0f8f9 c0f8a4 c0f8b0 c0f899 c0f892 c0f882 c0f8f8 c0f880 c0f890 c080c0 c080f9 c080a4 c080b0
  //   c08099 c08092 c08082 c080f8 c08080 c08090 c090c0 c090f9 c090a4 c090b0 c09099 c09092 c09082 c090f8
  //   c09080 c09090 f9c0c0 f9c0f9 f9c0a4 f9c0b0 f9c099 f9c092 f9c082 f9c0f8 f9c080 f9c090 f9f9c0 f9f9f9
  //   f9f9a4 f9f9b0 f9f999 f9f992 f9f982 f9f9f8 f9f980 f9f990 f9a4c0 f9a4f9 f9a4a4 f9a4b0 f9a499 f9a492
  //   f9a482 f9a4f8 f9a480 f9a490 f9b0c0 f9b0f9 f9b0a4 f9b0b0 f9b099 f9b092 f9b082 f9b0f8 f9b080 f9b090
  //   f999c0 f999f9 f999a4 f999b0 f99999 f99992 f99982 f999f8 f99980 f99990 f992c0 f992f9 f992a4 f992b0
  //   f99299 f99292 f99282 f992f8 f99280 f99290 f982c0 f982f9 f982a4 f982b0 f98299 f98292 f98282 f982f8
  //   f98280 f98290 f9f8c0 f9f8f9 f9f8a4 f9f8b0 f9f899 f9f892 f9f882 f9f8f8 f9f880 f9f890 f980c0 f980f9
  //   f980a4 f980b0 f98099 f98092 f98082 f980f8 f98080 f98090 f990c0 f990f9 f990a4 f990b0 f99099 f99092
  //   f99082 f990f8 f99080 f99090 a4c0c0 a4c0f9 a4c0a4 a4c0b0 a4c099 a4c092 a4c082 a4c0f8 a4c080 a4c090
  //   a4f9c0 a4f9f9 a4f9a4 a4f9b0 a4f999 a4f992 a4f982 a4f9f8 a4f980 a4f990 a4a4c0 a4a4f9 a4a4a4 a4a4b0
  //   a4a499 a4a492 a4a482 a4a4f8 a4a480 a4a490 a4b0c0 a4b0f9 a4b0a4 a4b0b0 a4b099 a4b092 a4b082 a4b0f8
  //   a4b080 a4b090 a499c0 a499f9 a499a4 a499b0 a49999 a49992 a49982 a499f8 a49980 a49990 a492c0 a492f9
  //   a492a4 a492b0 a49299 a49292
endmodule
