// Logisim project Working_7segment_disp_with_IC.circ as structural Verilog: 1 circuit, main circuit main
module main (
  input  count_en,
  input  count_out_star,
  input  Load_star,
  input  [3:0] Load,
  output [7:0] out_5
);

  wire clock_1_out, n7400_1_pin3, n7400_1_pin8, n7400_1_pin11, n7408_1_pin3, n7408_1_pin6, n7408_1_pin8,
       n7408_1_pin11, n7408_2_pin3, n7408_2_pin6, n7411_1_pin6, n7411_1_pin8, n7411_1_pin12, n7432_1_pin3,
       n7432_1_pin6, n7432_1_pin8, n7432_1_pin11, n7432_2_pin2, n7432_2_pin3, n7432_2_pin6, n7432_2_pin11,
       n7432_3_pin3, n7432_3_pin6, n7432_3_pin11, n7432_4_pin3, n7432_4_pin6, n7432_4_pin11, n7432_5_pin3,
       n7432_5_pin6, n7432_5_pin8, n7432_5_pin11, n74161_1_pin8, n74161_1_pin16, n74245_1_pin1,
       n74245_1_pin11, n74245_1_pin12, n74245_1_pin13, n74245_1_pin14, n74245_1_pin18, n74245_1_pin20;

  Clock clock_1 (.out(clock_1_out));
  _74245 #(.ShowInternalStructure("true"), .VccGndPorts("true")) u_74245_1 (
    .pin1(n74245_1_pin1), .pin2(out_5[7]), .pin3(out_5[6]), .pin4(out_5[5]), .pin5(out_5[4]),
    .pin6(out_5[3]), .pin7(out_5[2]), .pin8(out_5[1]), .pin9(out_5[0]), .pin10(n74245_1_pin1),
    .pin20(n74245_1_pin20), .pin19(count_out_star), .pin18(n74245_1_pin18), .pin17(n74245_1_pin18),
    .pin16(n74245_1_pin18), .pin15(n74245_1_pin18), .pin14(n74245_1_pin14), .pin13(n74245_1_pin13),
    .pin12(n74245_1_pin12), .pin11(n74245_1_pin11));
  _7400 #(.ShowInternalStructure("true")) u_7400_1 (
    .pin1(out_5[2]), .pin2(out_5[2]), .pin3(n7400_1_pin3), .pin4(out_5[3]), .pin5(out_5[3]),
    .pin13(out_5[0]), .pin12(out_5[0]), .pin11(n7400_1_pin11), .pin10(out_5[1]), .pin9(out_5[1]),
    .pin8(n7400_1_pin8));  // open: pin6
  _7408 #(.ShowInternalStructure("true")) u_7408_1 (
    .pin1(n7400_1_pin8), .pin2(n7400_1_pin11), .pin3(n7408_1_pin3), .pin4(out_5[0]), .pin5(out_5[1]),
    .pin6(n7408_1_pin6), .pin13(n7400_1_pin3), .pin12(n7400_1_pin11), .pin11(n7408_1_pin11),
    .pin10(out_5[2]), .pin9(out_5[0]), .pin8(n7408_1_pin8));
  _7411 #(.ShowInternalStructure("true")) u_7411_1 (
    .pin1(n7400_1_pin8), .pin2(out_5[0]), .pin3(out_5[1]), .pin4(n7400_1_pin11), .pin5(n7400_1_pin11),
    .pin6(n7411_1_pin6), .pin13(out_5[2]), .pin12(n7411_1_pin12), .pin11(n7400_1_pin3), .pin10(out_5[1]),
    .pin9(out_5[1]), .pin8(n7411_1_pin8));
  _74161 #(.ShowInternalStructure("true"), .VccGndPorts("true")) u_74161_1 (
    .pin2(clock_1_out), .pin3(Load[0]), .pin4(Load[1]), .pin5(Load[2]), .pin6(Load[3]), .pin7(count_en),
    .pin8(n74161_1_pin8), .pin16(n74161_1_pin16), .pin14(n74245_1_pin11), .pin13(n74245_1_pin12),
    .pin12(n74245_1_pin13), .pin11(n74245_1_pin14), .pin10(count_en), .pin9(Load_star));  // open: pin1, pin15
  _7408 #(.ShowInternalStructure("true")) u_7408_2 (
    .pin1(out_5[2]), .pin2(n7400_1_pin8), .pin3(n7408_2_pin3), .pin4(out_5[2]), .pin5(n7400_1_pin11),
    .pin6(n7408_2_pin6));  // open: pin13, pin12, pin11, pin10, pin9, pin8
  _7432 #(.ShowInternalStructure("true")) u_7432_1 (
    .pin1(n7400_1_pin3), .pin2(n7408_1_pin3), .pin3(n7432_1_pin3), .pin4(n7432_1_pin3), .pin5(n7408_1_pin6),
    .pin6(n7432_1_pin6), .pin13(n7408_1_pin8), .pin12(n7408_1_pin11), .pin11(n7432_1_pin11),
    .pin10(out_5[1]), .pin9(out_5[3]), .pin8(n7432_1_pin8));
  _7432 #(.ShowInternalStructure("true")) u_7432_2 (
    .pin1(n7411_1_pin6), .pin2(n7432_2_pin2), .pin3(n7432_2_pin3), .pin4(n7432_2_pin3), .pin5(out_5[3]),
    .pin6(n7432_2_pin6), .pin13(n7411_1_pin12), .pin12(n7408_1_pin11), .pin11(n7432_2_pin11),
    .pin10(n7432_2_pin11), .pin9(n7411_1_pin8), .pin8(n7432_2_pin2));
  _7432 #(.ShowInternalStructure("true")) u_7432_3 (
    .pin1(n7408_1_pin3), .pin2(n7408_2_pin3), .pin3(n7432_3_pin3), .pin4(n7432_3_pin3), .pin5(n7408_2_pin6),
    .pin6(n7432_3_pin6), .pin13(n7432_3_pin6), .pin12(out_5[3]), .pin11(n7432_3_pin11));  // open: pin10, pin9, pin8
  _7432 #(.ShowInternalStructure("true")) u_7432_4 (
    .pin1(n7400_1_pin8), .pin2(out_5[2]), .pin3(n7432_4_pin3), .pin4(n7432_4_pin3), .pin5(out_5[0]),
    .pin6(n7432_4_pin6), .pin13(n7432_1_pin11), .pin12(n7432_1_pin8), .pin11(n7432_4_pin11));  // open: pin10, pin9, pin8
  _7432 #(.ShowInternalStructure("true")) u_7432_5 (
    .pin1(n7411_1_pin8), .pin2(n7408_2_pin3), .pin3(n7432_5_pin3), .pin4(n7432_5_pin3), .pin5(n7408_2_pin6),
    .pin6(n7432_5_pin6), .pin13(n7408_1_pin11), .pin12(n7411_1_pin6), .pin11(n7432_5_pin11),
    .pin10(n7432_5_pin6), .pin9(out_5[3]), .pin8(n7432_5_pin8));
  _7_Segment_Display u_7_segment_display_1 (
    .g(n7432_5_pin8), .f(n7432_3_pin11), .a(n7432_4_pin11), .b(n7432_1_pin6), .e(n7432_5_pin11),
    .d(n7432_2_pin6), .c(n7432_4_pin6));  // open: dp
  // also tied to GND on the sheet: {n74245_1_pin18, n74245_1_pin1, n74161_1_pin8}
  // also tied to VCC on the sheet: {n74245_1_pin20, n74161_1_pin16}

  // Notes on the sheet:
  //   D
  //   C
  //   B
  //   A
  //   B*D*
  //   b
  //   d
  //   C*D*
  //   B*C
  //   BC*
  //   Combinationnal logic circuit
  //   f
  //   a
  //   CD*
  //   e
  //   c
  //   g
endmodule
