// Logisim project 7segment_dis_working_model_with_Counter.circ as structural Verilog: 1 circuit, main circuit main
module main (
  input  [3:0] in_1,
  input  count_en,
  input  count_out_star,
  input  Load_star,
  input  [3:0] Load,
  output [7:0] out_6
);

  wire and_1_out, and_2_out, and_3_out, and_4_out, and_5_out, and_6_out, and_7_out, and_8_out, and_9_out,
       and_10_out, and_11_out, and_12_out, and_13_out, and_14_out, and_15_out, and_16_out, clock_1_out,
       n74161_1_pin8, n74161_1_pin16, n74245_1_pin1, n74245_1_pin11, n74245_1_pin12, n74245_1_pin13,
       n74245_1_pin14, n74245_1_pin18, n74245_1_pin20, not_1_out, not_2_out, not_3_out, not_4_out, or_1_out,
       or_2_out, or_3_out, or_4_out, or_5_out, or_6_out, or_7_out;

  not not_1 (not_1_out, out_6[3]);
  not not_2 (not_2_out, out_6[0]);
  not not_3 (not_3_out, out_6[1]);
  not not_4 (not_4_out, out_6[2]);
  and and_1 (and_1_out, not_4_out, not_2_out);
  and and_2 (and_2_out, out_6[2], out_6[0]);
  and and_3 (and_3_out, not_3_out, not_2_out);
  and and_4 (and_4_out, out_6[1], out_6[0]);
  and and_5 (and_5_out, not_4_out, not_2_out);
  and and_6 (and_6_out, not_4_out, out_6[1]);
  and and_7 (and_7_out, out_6[2], not_3_out, out_6[0]);
  and and_8 (and_8_out, not_4_out, not_2_out);
  and and_9 (and_9_out, out_6[1], not_2_out);
  and and_10 (and_10_out, not_3_out, not_2_out);
  and and_11 (and_11_out, out_6[2], not_3_out);
  and and_12 (and_12_out, out_6[2], not_2_out);
  and and_13 (and_13_out, not_4_out, out_6[1]);
  and and_14 (and_14_out, out_6[2], not_3_out);
  and and_15 (and_15_out, out_6[2], not_2_out);
  or or_1 (or_1_out, not_3_out, out_6[0], out_6[2]);
  and and_16 (and_16_out, out_6[1], not_2_out);
  or or_2 (or_2_out, and_8_out, and_9_out);
  or or_3 (or_3_out, out_6[1], and_1_out, and_2_out, out_6[3]);
  or or_4 (or_4_out, not_4_out, and_3_out, and_4_out);
  or or_5 (or_5_out, and_6_out, and_7_out, out_6[3], and_5_out, and_16_out);
  or or_6 (or_6_out, and_10_out, and_11_out, and_12_out, out_6[3]);
  or or_7 (or_7_out, and_13_out, and_14_out, out_6[3], and_15_out);
  _7_Segment_Display u_7_segment_display_1 (
    .g(or_7_out), .f(or_6_out), .a(or_3_out), .b(or_4_out), .e(or_2_out), .d(or_5_out), .c(or_1_out));  // open: dp
  Clock clock_1 (.out(clock_1_out));
  _74245 #(.ShowInternalStructure("true"), .VccGndPorts("true")) u_74245_1 (
    .pin1(n74245_1_pin1), .pin2(out_6[7]), .pin3(out_6[6]), .pin4(out_6[5]), .pin5(out_6[4]),
    .pin6(out_6[3]), .pin7(out_6[2]), .pin8(out_6[1]), .pin9(out_6[0]), .pin10(n74245_1_pin1),
    .pin20(n74245_1_pin20), .pin19(count_out_star), .pin18(n74245_1_pin18), .pin17(n74245_1_pin18),
    .pin16(n74245_1_pin18), .pin15(n74245_1_pin18), .pin14(n74245_1_pin14), .pin13(n74245_1_pin13),
    .pin12(n74245_1_pin12), .pin11(n74245_1_pin11));
  _74161 #(.ShowInternalStructure("true"), .VccGndPorts("true")) u_74161_1 (
    .pin2(clock_1_out), .pin3(Load[0]), .pin4(Load[1]), .pin5(Load[2]), .pin6(Load[3]), .pin7(count_en),
    .pin8(n74161_1_pin8), .pin16(n74161_1_pin16), .pin14(n74245_1_pin11), .pin13(n74245_1_pin12),
    .pin12(n74245_1_pin13), .pin11(n74245_1_pin14), .pin10(count_en), .pin9(Load_star));  // open: pin1, pin15
  // also tied to GND on the sheet: {n74245_1_pin18, n74245_1_pin1, n74161_1_pin8}
  // also tied to VCC on the sheet: {n74245_1_pin20, n74161_1_pin16}

  // Notes on the sheet:
  //   D
  //   C
  //   B
  //   A
  //   7 segment display
  //   a
  //   b
  //   c
  //   d
  //   e
  //   f
  //   g
  //   B*D* + C + BD + A
  //   B* + C*D* + CD
  //   C* + B + D
  //   B*D*+B*C+BC*D+CD*+A
  //   B*D*+CD*
  //   C*D*+BC*+BD*+A
  //   B*C+BC*+A+BD*
endmodule
