// Logisim project 7segment_disp_Woring_Model_using_Rom.circ as structural Verilog: 1 circuit, main circuit main
module main (
  input  count_en,
  input  count_out_star,
  input  Load_star,
  input  [3:0] Load,
  input  [3:0] in_5,
  output [7:0] out_6,
  output [7:0] out_7
);

  wire clock_1_out, n74161_1_pin8, n74161_1_pin16, n74245_1_pin1, n74245_1_pin11, n74245_1_pin12,
       n74245_1_pin13, n74245_1_pin14, n74245_1_pin18, n74245_1_pin20;

  _74245 #(.ShowInternalStructure("true"), .VccGndPorts("true")) u_74245_1 (
    .pin1(n74245_1_pin1), .pin2(out_6[7]), .pin3(out_6[6]), .pin4(out_6[5]), .pin5(out_6[4]),
    .pin6(out_6[3]), .pin7(out_6[2]), .pin8(out_6[1]), .pin9(out_6[0]), .pin10(n74245_1_pin1),
    .pin20(n74245_1_pin20), .pin19(count_out_star), .pin18(n74245_1_pin18), .pin17(n74245_1_pin18),
    .pin16(n74245_1_pin18), .pin15(n74245_1_pin18), .pin14(n74245_1_pin14), .pin13(n74245_1_pin13),
    .pin12(n74245_1_pin12), .pin11(n74245_1_pin11));
  Clock clock_1 (.out(clock_1_out));
  LED led_1 (.in(out_6[3]));
  LED led_2 (.in(out_6[2]));
  LED led_3 (.in(out_6[1]));
  _74161 #(.ShowInternalStructure("true"), .VccGndPorts("true")) u_74161_1 (
    .pin2(clock_1_out), .pin3(Load[0]), .pin4(Load[1]), .pin5(Load[2]), .pin6(Load[3]), .pin7(count_en),
    .pin8(n74161_1_pin8), .pin16(n74161_1_pin16), .pin14(n74245_1_pin11), .pin13(n74245_1_pin12),
    .pin12(n74245_1_pin13), .pin11(n74245_1_pin14), .pin10(count_en), .pin9(Load_star));  // open: pin1, pin15
  LED led_4 (.in(out_6[0]));
  ROM #(.addrWidth(4)) rom_1 (.addr(out_6[3:0]), .data(out_7));
  _7_Segment_Display #(.active("false")) u_7_segment_display_1 (
    .g(out_7[6]), .f(out_7[5]), .a(out_7[0]), .b(out_7[1]), .e(out_7[4]), .d(out_7[3]), .c(out_7[2]),
    .dp(out_7[7]));
  // also tied to GND on the sheet: {n74245_1_pin18, n74245_1_pin1, n74161_1_pin8}
  // also tied to VCC on the sheet: {n74245_1_pin20, n74161_1_pin16}

  // Notes on the sheet:
  //   contents of rom_1 (hex, n*v repeats v):
  //   c0 f9 a4 b0 99 92 82 f8 80 90 88 83 c6 a1 86 8e
endmodule
