// Logisim project 8Byte_Static_Ram_Working_Model.circ as structural Verilog: 1 circuit, main circuit main
module main (
  input  [7:0] in_1,
  input  [3:0] in_2,
  input  out,
  input  load,
  input  load_2,
  input  en,
  input  enable_star
);

  wire and_1_out, and_2_out, and_3_out, and_4_out, and_5_out, and_6_out, and_7_out, and_8_out, and_9_out,
       and_10_out, and_11_out, and_12_out, and_13_out, and_14_out, and_15_out, and_16_out, button_1_out,
       clock_1_out, clock_2_out, decoder_1_out0, decoder_1_out1, decoder_1_out2, decoder_1_out3,
       decoder_1_out4, decoder_1_out5, decoder_1_out6, decoder_1_out7, decoder_1_out8, decoder_1_out9,
       decoder_1_out10, decoder_1_out11, decoder_1_out12, decoder_1_out13, decoder_1_out14, decoder_1_out15,
       n74245_1_pin1, n74245_1_pin10, n74245_1_pin19, n74245_2_pin19, n74245_3_pin19, n74245_4_pin19,
       n74245_5_pin19, n74245_6_pin19, n74245_7_pin19, n74245_8_pin19, n74245_9_pin19, n74245_10_pin19,
       n74245_11_pin19, n74245_12_pin19, n74245_13_pin19, n74245_14_pin19, n74245_15_pin19, n74245_16_pin19,
       n74245_17_pin1, n74245_17_pin10;
  wire [7:0] n74245_1_pin18, register_1_q, register_2_q, register_3_q, register_4_q, register_5_q,
       register_6_q, register_7_q, register_8_q, register_9_q, register_10_q, register_11_q, register_12_q,
       register_13_q, register_14_q, register_15_q, register_16_q, register_17_q;

  Register register_1 (.D(n74245_1_pin18), .en(and_1_out), .clk(clock_1_out), .Q(register_1_q));  // open: clr
  Register register_2 (.D(n74245_1_pin18), .en(and_2_out), .clk(clock_1_out), .Q(register_2_q));  // open: clr
  Register register_3 (.D(n74245_1_pin18), .en(and_3_out), .clk(clock_1_out), .Q(register_3_q));  // open: clr
  Register register_4 (.D(n74245_1_pin18), .en(and_4_out), .clk(clock_1_out), .Q(register_4_q));  // open: clr
  Register register_5 (.D(n74245_1_pin18), .en(and_5_out), .clk(clock_1_out), .Q(register_5_q));  // open: clr
  Register register_6 (.D(n74245_1_pin18), .en(and_6_out), .clk(clock_1_out), .Q(register_6_q));  // open: clr
  Register register_7 (.D(n74245_1_pin18), .en(and_7_out), .clk(clock_1_out), .Q(register_7_q));  // open: clr
  Register register_8 (.D(n74245_1_pin18), .en(and_8_out), .clk(clock_1_out), .Q(register_8_q));  // open: clr
  Register register_9 (.D(n74245_1_pin18), .en(and_9_out), .clk(clock_1_out), .Q(register_9_q));  // open: clr
  Register register_10 (.D(n74245_1_pin18), .en(and_10_out), .clk(clock_1_out), .Q(register_10_q));  // open: clr
  Register register_11 (.D(n74245_1_pin18), .en(and_11_out), .clk(clock_1_out), .Q(register_11_q));  // open: clr
  Register register_12 (.D(n74245_1_pin18), .en(and_12_out), .clk(clock_1_out), .Q(register_12_q));  // open: clr
  Register register_13 (.D(n74245_1_pin18), .en(and_13_out), .clk(clock_1_out), .Q(register_13_q));  // open: clr
  Register register_14 (.D(n74245_1_pin18), .en(and_14_out), .clk(clock_1_out), .Q(register_14_q));  // open: clr
  Register register_15 (.D(n74245_1_pin18), .en(and_15_out), .clk(clock_1_out), .Q(register_15_q));  // open: clr
  Register register_16 (.D(n74245_1_pin18), .en(and_16_out), .clk(clock_1_out), .Q(register_16_q));  // open: clr
  _74245 #(.ShowInternalStructure("true"), .VccGndPorts("true")) u_74245_1 (
    .pin1(n74245_1_pin1), .pin2(register_1_q[0]), .pin3(register_1_q[1]), .pin4(register_1_q[2]),
    .pin5(register_1_q[3]), .pin6(register_1_q[4]), .pin7(register_1_q[5]), .pin8(register_1_q[6]),
    .pin9(register_1_q[7]), .pin10(n74245_1_pin10), .pin20(n74245_1_pin1), .pin19(n74245_1_pin19),
    .pin18(n74245_1_pin18[0]), .pin17(n74245_1_pin18[1]), .pin16(n74245_1_pin18[2]),
    .pin15(n74245_1_pin18[3]), .pin14(n74245_1_pin18[4]), .pin13(n74245_1_pin18[5]),
    .pin12(n74245_1_pin18[6]), .pin11(n74245_1_pin18[7]));
  _74245 #(.ShowInternalStructure("true"), .VccGndPorts("true")) u_74245_2 (
    .pin1(n74245_1_pin1), .pin2(register_2_q[0]), .pin3(register_2_q[1]), .pin4(register_2_q[2]),
    .pin5(register_2_q[3]), .pin6(register_2_q[4]), .pin7(register_2_q[5]), .pin8(register_2_q[6]),
    .pin9(register_2_q[7]), .pin10(n74245_1_pin10), .pin20(n74245_1_pin1), .pin19(n74245_2_pin19),
    .pin18(n74245_1_pin18[0]), .pin17(n74245_1_pin18[1]), .pin16(n74245_1_pin18[2]),
    .pin15(n74245_1_pin18[3]), .pin14(n74245_1_pin18[4]), .pin13(n74245_1_pin18[5]),
    .pin12(n74245_1_pin18[6]), .pin11(n74245_1_pin18[7]));
  _74245 #(.ShowInternalStructure("true"), .VccGndPorts("true")) u_74245_3 (
    .pin1(n74245_1_pin1), .pin2(register_3_q[0]), .pin3(register_3_q[1]), .pin4(register_3_q[2]),
    .pin5(register_3_q[3]), .pin6(register_3_q[4]), .pin7(register_3_q[5]), .pin8(register_3_q[6]),
    .pin9(register_3_q[7]), .pin10(n74245_1_pin10), .pin20(n74245_1_pin1), .pin19(n74245_3_pin19),
    .pin18(n74245_1_pin18[0]), .pin17(n74245_1_pin18[1]), .pin16(n74245_1_pin18[2]),
    .pin15(n74245_1_pin18[3]), .pin14(n74245_1_pin18[4]), .pin13(n74245_1_pin18[5]),
    .pin12(n74245_1_pin18[6]), .pin11(n74245_1_pin18[7]));
  _74245 #(.ShowInternalStructure("true"), .VccGndPorts("true")) u_74245_4 (
    .pin1(n74245_1_pin1), .pin2(register_4_q[0]), .pin3(register_4_q[1]), .pin4(register_4_q[2]),
    .pin5(register_4_q[3]), .pin6(register_4_q[4]), .pin7(register_4_q[5]), .pin8(register_4_q[6]),
    .pin9(register_4_q[7]), .pin10(n74245_1_pin10), .pin20(n74245_1_pin1), .pin19(n74245_4_pin19),
    .pin18(n74245_1_pin18[0]), .pin17(n74245_1_pin18[1]), .pin16(n74245_1_pin18[2]),
    .pin15(n74245_1_pin18[3]), .pin14(n74245_1_pin18[4]), .pin13(n74245_1_pin18[5]),
    .pin12(n74245_1_pin18[6]), .pin11(n74245_1_pin18[7]));
  _74245 #(.ShowInternalStructure("true"), .VccGndPorts("true")) u_74245_5 (
    .pin1(n74245_1_pin1), .pin2(register_5_q[0]), .pin3(register_5_q[1]), .pin4(register_5_q[2]),
    .pin5(register_5_q[3]), .pin6(register_5_q[4]), .pin7(register_5_q[5]), .pin8(register_5_q[6]),
    .pin9(register_5_q[7]), .pin10(n74245_1_pin10), .pin20(n74245_1_pin1), .pin19(n74245_5_pin19),
    .pin18(n74245_1_pin18[0]), .pin17(n74245_1_pin18[1]), .pin16(n74245_1_pin18[2]),
    .pin15(n74245_1_pin18[3]), .pin14(n74245_1_pin18[4]), .pin13(n74245_1_pin18[5]),
    .pin12(n74245_1_pin18[6]), .pin11(n74245_1_pin18[7]));
  _74245 #(.ShowInternalStructure("true"), .VccGndPorts("true")) u_74245_6 (
    .pin1(n74245_1_pin1), .pin2(register_6_q[0]), .pin3(register_6_q[1]), .pin4(register_6_q[2]),
    .pin5(register_6_q[3]), .pin6(register_6_q[4]), .pin7(register_6_q[5]), .pin8(register_6_q[6]),
    .pin9(register_6_q[7]), .pin10(n74245_1_pin10), .pin20(n74245_1_pin1), .pin19(n74245_6_pin19),
    .pin18(n74245_1_pin18[0]), .pin17(n74245_1_pin18[1]), .pin16(n74245_1_pin18[2]),
    .pin15(n74245_1_pin18[3]), .pin14(n74245_1_pin18[4]), .pin13(n74245_1_pin18[5]),
    .pin12(n74245_1_pin18[6]), .pin11(n74245_1_pin18[7]));
  _74245 #(.ShowInternalStructure("true"), .VccGndPorts("true")) u_74245_7 (
    .pin1(n74245_1_pin1), .pin2(register_7_q[0]), .pin3(register_7_q[1]), .pin4(register_7_q[2]),
    .pin5(register_7_q[3]), .pin6(register_7_q[4]), .pin7(register_7_q[5]), .pin8(register_7_q[6]),
    .pin9(register_7_q[7]), .pin10(n74245_1_pin10), .pin20(n74245_1_pin1), .pin19(n74245_7_pin19),
    .pin18(n74245_1_pin18[0]), .pin17(n74245_1_pin18[1]), .pin16(n74245_1_pin18[2]),
    .pin15(n74245_1_pin18[3]), .pin14(n74245_1_pin18[4]), .pin13(n74245_1_pin18[5]),
    .pin12(n74245_1_pin18[6]), .pin11(n74245_1_pin18[7]));
  _74245 #(.ShowInternalStructure("true"), .VccGndPorts("true")) u_74245_8 (
    .pin1(n74245_1_pin1), .pin2(register_8_q[0]), .pin3(register_8_q[1]), .pin4(register_8_q[2]),
    .pin5(register_8_q[3]), .pin6(register_8_q[4]), .pin7(register_8_q[5]), .pin8(register_8_q[6]),
    .pin9(register_8_q[7]), .pin10(n74245_1_pin10), .pin20(n74245_1_pin1), .pin19(n74245_8_pin19),
    .pin18(n74245_1_pin18[0]), .pin17(n74245_1_pin18[1]), .pin16(n74245_1_pin18[2]),
    .pin15(n74245_1_pin18[3]), .pin14(n74245_1_pin18[4]), .pin13(n74245_1_pin18[5]),
    .pin12(n74245_1_pin18[6]), .pin11(n74245_1_pin18[7]));
  _74245 #(.ShowInternalStructure("true"), .VccGndPorts("true")) u_74245_9 (
    .pin1(n74245_1_pin1), .pin2(register_9_q[0]), .pin3(register_9_q[1]), .pin4(register_9_q[2]),
    .pin5(register_9_q[3]), .pin6(register_9_q[4]), .pin7(register_9_q[5]), .pin8(register_9_q[6]),
    .pin9(register_9_q[7]), .pin10(n74245_1_pin10), .pin20(n74245_1_pin1), .pin19(n74245_9_pin19),
    .pin18(n74245_1_pin18[0]), .pin17(n74245_1_pin18[1]), .pin16(n74245_1_pin18[2]),
    .pin15(n74245_1_pin18[3]), .pin14(n74245_1_pin18[4]), .pin13(n74245_1_pin18[5]),
    .pin12(n74245_1_pin18[6]), .pin11(n74245_1_pin18[7]));
  _74245 #(.ShowInternalStructure("true"), .VccGndPorts("true")) u_74245_10 (
    .pin1(n74245_1_pin1), .pin2(register_10_q[0]), .pin3(register_10_q[1]), .pin4(register_10_q[2]),
    .pin5(register_10_q[3]), .pin6(register_10_q[4]), .pin7(register_10_q[5]), .pin8(register_10_q[6]),
    .pin9(register_10_q[7]), .pin10(n74245_1_pin10), .pin20(n74245_1_pin1), .pin19(n74245_10_pin19),
    .pin18(n74245_1_pin18[0]), .pin17(n74245_1_pin18[1]), .pin16(n74245_1_pin18[2]),
    .pin15(n74245_1_pin18[3]), .pin14(n74245_1_pin18[4]), .pin13(n74245_1_pin18[5]),
    .pin12(n74245_1_pin18[6]), .pin11(n74245_1_pin18[7]));
  _74245 #(.ShowInternalStructure("true"), .VccGndPorts("true")) u_74245_11 (
    .pin1(n74245_1_pin1), .pin2(register_11_q[0]), .pin3(register_11_q[1]), .pin4(register_11_q[2]),
    .pin5(register_11_q[3]), .pin6(register_11_q[4]), .pin7(register_11_q[5]), .pin8(register_11_q[6]),
    .pin9(register_11_q[7]), .pin10(n74245_1_pin10), .pin20(n74245_1_pin1), .pin19(n74245_11_pin19),
    .pin18(n74245_1_pin18[0]), .pin17(n74245_1_pin18[1]), .pin16(n74245_1_pin18[2]),
    .pin15(n74245_1_pin18[3]), .pin14(n74245_1_pin18[4]), .pin13(n74245_1_pin18[5]),
    .pin12(n74245_1_pin18[6]), .pin11(n74245_1_pin18[7]));
  _74245 #(.ShowInternalStructure("true"), .VccGndPorts("true")) u_74245_12 (
    .pin1(n74245_1_pin1), .pin2(register_12_q[0]), .pin3(register_12_q[1]), .pin4(register_12_q[2]),
    .pin5(register_12_q[3]), .pin6(register_12_q[4]), .pin7(register_12_q[5]), .pin8(register_12_q[6]),
    .pin9(register_12_q[7]), .pin10(n74245_1_pin10), .pin20(n74245_1_pin1), .pin19(n74245_12_pin19),
    .pin18(n74245_1_pin18[0]), .pin17(n74245_1_pin18[1]), .pin16(n74245_1_pin18[2]),
    .pin15(n74245_1_pin18[3]), .pin14(n74245_1_pin18[4]), .pin13(n74245_1_pin18[5]),
    .pin12(n74245_1_pin18[6]), .pin11(n74245_1_pin18[7]));
  _74245 #(.ShowInternalStructure("true"), .VccGndPorts("true")) u_74245_13 (
    .pin1(n74245_1_pin1), .pin2(register_13_q[0]), .pin3(register_13_q[1]), .pin4(register_13_q[2]),
    .pin5(register_13_q[3]), .pin6(register_13_q[4]), .pin7(register_13_q[5]), .pin8(register_13_q[6]),
    .pin9(register_13_q[7]), .pin10(n74245_1_pin10), .pin20(n74245_1_pin1), .pin19(n74245_13_pin19),
    .pin18(n74245_1_pin18[0]), .pin17(n74245_1_pin18[1]), .pin16(n74245_1_pin18[2]),
    .pin15(n74245_1_pin18[3]), .pin14(n74245_1_pin18[4]), .pin13(n74245_1_pin18[5]),
    .pin12(n74245_1_pin18[6]), .pin11(n74245_1_pin18[7]));
  _74245 #(.ShowInternalStructure("true"), .VccGndPorts("true")) u_74245_14 (
    .pin1(n74245_1_pin1), .pin2(register_14_q[0]), .pin3(register_14_q[1]), .pin4(register_14_q[2]),
    .pin5(register_14_q[3]), .pin6(register_14_q[4]), .pin7(register_14_q[5]), .pin8(register_14_q[6]),
    .pin9(register_14_q[7]), .pin10(n74245_1_pin10), .pin20(n74245_1_pin1), .pin19(n74245_14_pin19),
    .pin18(n74245_1_pin18[0]), .pin17(n74245_1_pin18[1]), .pin16(n74245_1_pin18[2]),
    .pin15(n74245_1_pin18[3]), .pin14(n74245_1_pin18[4]), .pin13(n74245_1_pin18[5]),
    .pin12(n74245_1_pin18[6]), .pin11(n74245_1_pin18[7]));
  _74245 #(.ShowInternalStructure("true"), .VccGndPorts("true")) u_74245_15 (
    .pin1(n74245_1_pin1), .pin2(register_15_q[0]), .pin3(register_15_q[1]), .pin4(register_15_q[2]),
    .pin5(register_15_q[3]), .pin6(register_15_q[4]), .pin7(register_15_q[5]), .pin8(register_15_q[6]),
    .pin9(register_15_q[7]), .pin10(n74245_1_pin10), .pin20(n74245_1_pin1), .pin19(n74245_15_pin19),
    .pin18(n74245_1_pin18[0]), .pin17(n74245_1_pin18[1]), .pin16(n74245_1_pin18[2]),
    .pin15(n74245_1_pin18[3]), .pin14(n74245_1_pin18[4]), .pin13(n74245_1_pin18[5]),
    .pin12(n74245_1_pin18[6]), .pin11(n74245_1_pin18[7]));
  _74245 #(.ShowInternalStructure("true"), .VccGndPorts("true")) u_74245_16 (
    .pin1(n74245_1_pin1), .pin2(register_16_q[0]), .pin3(register_16_q[1]), .pin4(register_16_q[2]),
    .pin5(register_16_q[3]), .pin6(register_16_q[4]), .pin7(register_16_q[5]), .pin8(register_16_q[6]),
    .pin9(register_16_q[7]), .pin10(n74245_1_pin10), .pin20(n74245_1_pin1), .pin19(n74245_16_pin19),
    .pin18(n74245_1_pin18[0]), .pin17(n74245_1_pin18[1]), .pin16(n74245_1_pin18[2]),
    .pin15(n74245_1_pin18[3]), .pin14(n74245_1_pin18[4]), .pin13(n74245_1_pin18[5]),
    .pin12(n74245_1_pin18[6]), .pin11(n74245_1_pin18[7]));
  nand nand_1 (n74245_1_pin19, out, decoder_1_out0);
  and and_1 (and_1_out, load_2, decoder_1_out0);
  nand nand_2 (n74245_2_pin19, out, decoder_1_out1);
  and and_2 (and_2_out, load_2, decoder_1_out1);
  nand nand_3 (n74245_3_pin19, out, decoder_1_out2);
  and and_3 (and_3_out, load_2, decoder_1_out2);
  nand nand_4 (n74245_4_pin19, out, decoder_1_out3);
  and and_4 (and_4_out, load_2, decoder_1_out3);
  nand nand_5 (n74245_5_pin19, out, decoder_1_out4);
  and and_5 (and_5_out, load_2, decoder_1_out4);
  nand nand_6 (n74245_6_pin19, out, decoder_1_out5);
  and and_6 (and_6_out, load_2, decoder_1_out5);
  nand nand_7 (n74245_7_pin19, out, decoder_1_out6);
  and and_7 (and_7_out, load_2, decoder_1_out6);
  nand nand_8 (n74245_8_pin19, out, decoder_1_out7);
  and and_8 (and_8_out, load_2, decoder_1_out7);
  nand nand_9 (n74245_9_pin19, out, decoder_1_out8);
  and and_9 (and_9_out, load_2, decoder_1_out8);
  nand nand_10 (n74245_10_pin19, out, decoder_1_out9);
  and and_10 (and_10_out, load_2, decoder_1_out9);
  nand nand_11 (n74245_11_pin19, out, decoder_1_out10);
  and and_11 (and_11_out, load_2, decoder_1_out10);
  nand nand_12 (n74245_12_pin19, out, decoder_1_out11);
  and and_12 (and_12_out, load_2, decoder_1_out11);
  nand nand_13 (n74245_13_pin19, out, decoder_1_out12);
  and and_13 (and_13_out, load_2, decoder_1_out12);
  nand nand_14 (n74245_14_pin19, out, decoder_1_out13);
  and and_14 (and_14_out, load_2, decoder_1_out13);
  nand nand_15 (n74245_15_pin19, out, decoder_1_out14);
  and and_15 (and_15_out, load_2, decoder_1_out14);
  nand nand_16 (n74245_16_pin19, out, decoder_1_out15);
  and and_16 (and_16_out, load_2, decoder_1_out15);
  Decoder #(.disabled("Z"), .select(4)) decoder_1 (
    .out0(decoder_1_out0), .out1(decoder_1_out1), .out2(decoder_1_out2), .out3(decoder_1_out3),
    .out4(decoder_1_out4), .out5(decoder_1_out5), .out6(decoder_1_out6), .out7(decoder_1_out7),
    .out8(decoder_1_out8), .out9(decoder_1_out9), .out10(decoder_1_out10), .out11(decoder_1_out11),
    .out12(decoder_1_out12), .out13(decoder_1_out13), .out14(decoder_1_out14), .out15(decoder_1_out15),
    .sel(in_2), .en(en));
  LED led_1 (.in(n74245_1_pin18[0]));
  LED led_2 (.in(n74245_1_pin18[1]));
  LED led_3 (.in(n74245_1_pin18[2]));
  LED led_4 (.in(n74245_1_pin18[3]));
  LED led_5 (.in(n74245_1_pin18[4]));
  LED led_6 (.in(n74245_1_pin18[5]));
  LED led_7 (.in(n74245_1_pin18[6]));
  LED led_8 (.in(n74245_1_pin18[7]));
  Clock clock_1 (.out(clock_1_out));
  Register register_17 (.D(in_1), .en(load), .clk(clock_2_out), .Q(register_17_q), .clr(button_1_out));
  Clock clock_2 (.out(clock_2_out));
  LED led_9 (.in(clock_2_out));
  Button button_1 (.out(button_1_out));
  LED led_10 (.in(register_17_q[0]));
  LED led_11 (.in(register_17_q[1]));
  LED led_12 (.in(register_17_q[2]));
  LED led_13 (.in(register_17_q[3]));
  LED led_14 (.in(register_17_q[4]));
  LED led_15 (.in(register_17_q[5]));
  LED led_16 (.in(register_17_q[6]));
  LED led_17 (.in(register_17_q[7]));
  _74245 #(.VccGndPorts("true")) u_74245_17 (
    .pin1(n74245_17_pin1), .pin2(register_17_q[0]), .pin3(register_17_q[1]), .pin4(register_17_q[2]),
    .pin5(register_17_q[3]), .pin6(register_17_q[4]), .pin7(register_17_q[5]), .pin8(register_17_q[6]),
    .pin9(register_17_q[7]), .pin10(n74245_17_pin10), .pin20(n74245_17_pin1), .pin19(enable_star),
    .pin18(n74245_1_pin18[0]), .pin17(n74245_1_pin18[1]), .pin16(n74245_1_pin18[2]),
    .pin15(n74245_1_pin18[3]), .pin14(n74245_1_pin18[4]), .pin13(n74245_1_pin18[5]),
    .pin12(n74245_1_pin18[6]), .pin11(n74245_1_pin18[7]));
  // also tied to GND on the sheet: {n74245_1_pin10, n74245_17_pin10}
  // also tied to VCC on the sheet: {n74245_1_pin1, n74245_17_pin1}

  // Notes on the sheet:
  //   8 Byte Static Ram Working Model
  //   vcc
  //   vcc
  //   vcc
  //   vcc
  //   vcc
  //   vcc
  //   vcc
  //   vcc
  //   vcc
  //   vcc
  //   vcc
  //   vcc
  //   vcc
  //   vcc
  //   vcc
  //   vcc
  //   GND
  //   GND
  //   GND
  //   GND
  //   GND
  //   GND
  //   GND
  //   GND
  //   GND
  //   GND
  //   GND
  //   GND
  //   GND
  //   GND
  //   GND
  //   GND
  //   bus
  //   en*
  //   clk
  //   load
  //   bus
  //   clk
  //   load
  //   bus
  //   clk
  //   load
  //   bus
  //   clk
  //   load
  //   bus
  //   clk
  //   load
  //   bus
  //   clk
  //   load
  //   bus
  //   clk
  //   load
  //   bus
  //   clk
  //   load
  //   bus
  //   clk
  //   load
  //   bus
  //   clk
  //   load
  //   bus
  //   clk
  //   load
  //   bus
  //   clk
  //   load
  //   bus
  //   clk
  //   load
  //   bus
  //   clk
  //   load
  //   bus
  //   clk
  //   load
  //   bus
  //   clk
  //   load
  //   load En
  //   out en
  //   bus
  //   add..
  //   8 bit bus
  //   clr
endmodule
