// Logisim project Bus_input_system_IC74245.circ as structural Verilog: 1 circuit, main circuit main
module main (
  input  [7:0] in_1,
  input  M,
  input  En,
  input  A,
  input  B,
  input  C,
  output [7:0] bus_out
);

  wire clock_1_out, n74245_1_pin1, n74245_1_pin10, n74245_1_pin20;
  wire [7:0] register_2_q, register_3_q, register_4_q;

  Clock clock_1 (.out(clock_1_out));
  Register register_1 (
    .D(in_1), .en(M), .clk(clock_1_out), .Q({bus_out[7:6], {4{bus_out[6]}}, bus_out[1:0]}));  // open: clr
  Register register_2 (
    .D({bus_out[7:6], {4{bus_out[6]}}, bus_out[1:0]}), .en(C), .clk(clock_1_out), .Q(register_2_q));  // open: clr
  Register register_3 (
    .D({bus_out[7:6], {4{bus_out[6]}}, bus_out[1:0]}), .en(B), .clk(clock_1_out), .Q(register_3_q));  // open: clr
  Register register_4 (
    .D({bus_out[7:6], {4{bus_out[6]}}, bus_out[1:0]}), .en(A), .clk(clock_1_out), .Q(register_4_q));  // open: clr
  _74245 #(.VccGndPorts("true")) u_74245_1 (
    .pin1(n74245_1_pin1), .pin2(bus_out[0]), .pin3(bus_out[1]), .pin4(bus_out[6]), .pin5(bus_out[6]),
    .pin6(bus_out[6]), .pin7(bus_out[6]), .pin8(bus_out[6]), .pin9(bus_out[7]), .pin10(n74245_1_pin10),
    .pin20(n74245_1_pin20), .pin19(En), .pin18(register_3_q[0]), .pin17(register_3_q[1]),
    .pin16(register_3_q[2]), .pin15(register_3_q[3]), .pin14(register_3_q[4]), .pin13(register_3_q[5]),
    .pin12(register_3_q[6]), .pin11(register_3_q[7]));

  assign bus_out[5:2] = {4{bus_out[6]}};
  // also tied to GND on the sheet: n74245_1_pin10
  // also tied to VCC on the sheet: n74245_1_pin20

  // Notes on the sheet:
  //   input
  //   C
  //   B
  //   A
  //   D  E 
  //   L  L  B to A
  //   L  H  A to B
  //   X  H  isolation
  //   Dir
  //   A..
  //   B..
endmodule
