// Logisim project N_P_Transistor.circ as structural Verilog: 1 circuit, main circuit main
module main (
  input  Ptype,
  input  Ntype,
  input  in_3,
  input  in_4
);

  wire transistor_1_out, transistor_2_out;

  Transistor transistor_1 (.in(in_3), .out(transistor_1_out), .gate(Ptype));
  LED led_1 (.in(transistor_1_out));
  Transistor #(.\type ("n")) transistor_2 (.in(in_4), .out(transistor_2_out), .gate(Ntype));
  LED led_2 (.in(transistor_2_out));

  // Notes on the sheet:
  //   s->1, g->0 , d=>1
  //   s->0, g->1 , d=>0
endmodule
